// Logisim project ciccio.circ as structural Verilog: 9 circuits, main circuit main
module main (
);

  wire _0_2_out, _0_out, _1_2_out, _1_out, _2_2_out, _2_out, _3_2_out, _3_out, _4_2_out, _4_out, _5_2_out,
       _5_out, A1, A2, A_2_out, A_out, and_1_out, and_2_out, and_3_out, B_2_out, B_out, button_2_out,
       button_out, C_2_out, C_out, clock, D_2_out, D_out, display_driver_1_a, display_driver_1_b,
       display_driver_1_c, display_driver_1_d, display_driver_1_i1, display_driver_1_out_5,
       display_driver_1_out_6, display_driver_1_out_7, display_driver_1_out_8, display_driver_1_out_9,
       display_driver_1_out_10, display_driver_1_out_11, display_driver_1_out_12, display_driver_1_out_13,
       display_driver_1_out_14, display_driver_1_out_15, display_driver_1_out_16, display_driver_1_out_17,
       display_driver_1_out_18, display_driver_1_out_19, display_driver_1_out_20, display_driver_1_out_21,
       display_driver_1_out_22, display_driver_1_out_23, display_driver_1_out_24, display_driver_1_out_25,
       display_driver_1_out_26, display_driver_1_out_27, display_driver_1_out_28, display_driver_1_out_29,
       display_driver_1_out_31, display_driver_1_out_32, display_driver_1_out_33, display_driver_1_out_34,
       display_driver_1_out_35, display_driver_1_out_37, display_driver_1_out_38, display_driver_1_out_39,
       display_driver_1_out_40, display_driver_1_out_41, display_driver_1_out_43, display_driver_1_out_44,
       display_driver_1_out_45, display_driver_1_out_46, display_driver_1_out_49, display_driver_1_out_50,
       display_driver_1_out_51, display_driver_1_out_52, display_driver_1_out_53, display_driver_1_out_54,
       display_driver_1_out_55, display_driver_1_out_56, display_driver_1_out_57, display_driver_1_out_58,
       display_driver_1_out_59, display_driver_1_out_60, display_driver_1_out_61, display_driver_1_out_62,
       display_driver_1_out_63, display_driver_1_out_64, display_driver_1_out_65, display_driver_1_out_66,
       display_driver_1_out_67, display_driver_1_out_68, display_driver_1_out_69, display_driver_1_out_70,
       display_driver_1_out_71, display_driver_1_out_72, display_driver_1_out_73, display_driver_1_out_74,
       display_driver_1_out_75, display_driver_1_out_76, display_driver_1_out_77, display_driver_1_out_78,
       display_driver_1_out_79, display_driver_1_out_80, display_driver_1_out_81, display_driver_1_out_82,
       display_driver_1_out_83, display_driver_1_out_84, display_driver_1_out_85, display_driver_1_out_86,
       display_driver_1_out_87, display_driver_1_out_88, display_driver_1_out_89, display_driver_1_out_90,
       display_driver_1_out_91, display_driver_1_out_92, display_driver_1_out_93, display_driver_1_out_94,
       display_driver_1_out_95, display_driver_1_out_96, display_driver_1_out_97, display_driver_1_out_98,
       display_driver_1_out_99, display_driver_1_out_100, display_driver_2_a, display_driver_2_b,
       display_driver_2_c, display_driver_2_d, display_driver_2_i1, display_driver_2_out_5,
       display_driver_2_out_6, display_driver_2_out_7, display_driver_2_out_8, display_driver_2_out_9,
       display_driver_2_out_10, display_driver_2_out_11, display_driver_2_out_12, display_driver_2_out_13,
       display_driver_2_out_14, display_driver_2_out_15, display_driver_2_out_16, display_driver_2_out_17,
       display_driver_2_out_18, display_driver_2_out_19, display_driver_2_out_20, display_driver_2_out_21,
       display_driver_2_out_22, display_driver_2_out_23, display_driver_2_out_24, display_driver_2_out_25,
       display_driver_2_out_26, display_driver_2_out_27, display_driver_2_out_28, display_driver_2_out_29,
       display_driver_2_out_31, display_driver_2_out_32, display_driver_2_out_33, display_driver_2_out_34,
       display_driver_2_out_35, display_driver_2_out_37, display_driver_2_out_38, display_driver_2_out_39,
       display_driver_2_out_40, display_driver_2_out_41, display_driver_2_out_43, display_driver_2_out_44,
       display_driver_2_out_45, display_driver_2_out_46, display_driver_2_out_49, display_driver_2_out_50,
       display_driver_2_out_51, display_driver_2_out_52, display_driver_2_out_53, display_driver_2_out_54,
       display_driver_2_out_55, display_driver_2_out_56, display_driver_2_out_57, display_driver_2_out_58,
       display_driver_2_out_59, display_driver_2_out_60, display_driver_2_out_61, display_driver_2_out_62,
       display_driver_2_out_63, display_driver_2_out_64, display_driver_2_out_65, display_driver_2_out_66,
       display_driver_2_out_67, display_driver_2_out_68, display_driver_2_out_69, display_driver_2_out_70,
       display_driver_2_out_71, display_driver_2_out_72, display_driver_2_out_73, display_driver_2_out_74,
       display_driver_2_out_75, display_driver_2_out_76, display_driver_2_out_77, display_driver_2_out_78,
       display_driver_2_out_79, display_driver_2_out_80, display_driver_2_out_81, display_driver_2_out_82,
       display_driver_2_out_83, display_driver_2_out_84, display_driver_2_out_85, display_driver_2_out_86,
       display_driver_2_out_87, display_driver_2_out_88, display_driver_2_out_89, display_driver_2_out_90,
       display_driver_2_out_91, display_driver_2_out_92, display_driver_2_out_93, display_driver_2_out_94,
       display_driver_2_out_95, display_driver_2_out_96, display_driver_2_out_97, display_driver_2_out_98,
       display_driver_2_out_99, display_driver_2_out_100, or_1_out, or_2_out, Reset, Reset_kp,
       shipcountmanager_1_player, Win;
  wire [1:0] attackprocessor_1_valueout, ReadOut;
  wire [2:0] S_C_1, S_C_2, shipcountmanager_1_out, statemanager_1_new_state, StateOut;
  wire [3:0] s_c_displaydriver_1_out, s_c_displaydriver_2_out;
  wire [4:0] S1, S2;
  wire [5:0] attackkeeper_1_out;
  wire [11:0] memory_1_d1_0, memory_1_d1_1, memory_1_d1_2, memory_1_d1_3, memory_1_d2_0, memory_1_d2_1,
       memory_1_d2_2, memory_1_d2_3;

  AttackKeeper attackkeeper_1 (.A1(S1), .A2(S2), .State(StateOut), .Out(attackkeeper_1_out));
  AttackProcessor attackprocessor_1 (.ValueIn(ReadOut), .ValueOut(attackprocessor_1_valueout), .State(StateOut));
  StateManager statemanager_1 (
    .A1(A1), .A2(A2), .State(StateOut), .S_C_1(S_C_1), .S_C_2(S_C_2), .New_State(statemanager_1_new_state),
    .Reset_key_pads(Reset_kp), .New_Game(Win));
  ShipCountManager shipcountmanager_1 (
    .Attack_Proc_or_Out(attackprocessor_1_valueout), .State(StateOut), .ShipCount1(S_C_1),
    .Player(shipcountmanager_1_player), .Out(shipcountmanager_1_out), .ShipCount2(S_C_2),
    .Current_value(ReadOut));
  and and_1 (and_1_out, clock, ~Reset);  // AND_Gate
  Clock clock_1 (.out(clock));
  Memory memory_1 (
    .State_write(statemanager_1_new_state), .B_C__Player_write(shipcountmanager_1_player),
    .Write_boat_count(shipcountmanager_1_out), .Read_out(ReadOut), .State_out(StateOut), .B_C__1_out(S_C_1),
    .B_C__2_out(S_C_2), .Register(attackkeeper_1_out), .Clock(and_1_out),
    .Write_content(attackprocessor_1_valueout), .D2_3(memory_1_d2_3), .D2_2(memory_1_d2_2),
    .D2_1(memory_1_d2_1), .D2_0(memory_1_d2_0), .D1_3(memory_1_d1_3), .D1_2(memory_1_d1_2),
    .D1_1(memory_1_d1_1), .D1_0(memory_1_d1_0), .Reset(Reset));
  or or_1 (or_1_out, Reset, Win, Reset_kp);
  LED led_1 (.in(display_driver_1_out_11));
  LED led_2 (.in(display_driver_1_out_17));
  LED led_3 (.in(display_driver_1_out_35));
  LED led_4 (.in(display_driver_1_out_41));
  LED led_5 (.in(display_driver_1_out_59));
  LED led_6 (.in(display_driver_1_out_65));
  LED led_7 (.in(display_driver_1_out_83));
  LED led_8 (.in(display_driver_1_out_89));
  LED led_9 (.in(display_driver_2_out_11));
  LED led_10 (.in(display_driver_2_out_17));
  LED led_11 (.in(display_driver_2_out_35));
  LED led_12 (.in(display_driver_2_out_41));
  LED led_13 (.in(display_driver_2_out_59));
  LED led_14 (.in(display_driver_2_out_65));
  LED led_15 (.in(display_driver_2_out_83));
  LED led_16 (.in(display_driver_2_out_89));
  or or_2 (or_2_out, Reset, Win, Reset_kp);
  Button A (.out(A_out));
  Button B (.out(B_out));
  Button C (.out(C_out));
  LED led_17 (.in(display_driver_1_out_6));
  LED led_18 (.in(display_driver_1_out_12));
  LED led_19 (.in(display_driver_1_out_5));
  LED led_20 (.in(display_driver_1_out_18));
  LED led_21 (.in(display_driver_1_out_24));
  LED led_22 (.in(display_driver_1_out_23));
  LED led_23 (.in(display_driver_1_out_29));
  LED led_24 (.in(display_driver_1_b));
  LED led_25 (.in(display_driver_1_a));
  LED led_26 (.in(display_driver_1_c));
  LED led_27 (.in(display_driver_1_i1));
  LED led_28 (.in(display_driver_1_d));
  LED led_29 (.in(display_driver_1_out_53));
  LED led_30 (.in(display_driver_1_out_60));
  LED led_31 (.in(display_driver_1_out_54));
  LED led_32 (.in(display_driver_1_out_72));
  LED led_33 (.in(display_driver_1_out_71));
  LED led_34 (.in(display_driver_1_out_66));
  LED led_35 (.in(display_driver_1_out_84));
  LED led_36 (.in(display_driver_1_out_78));
  LED led_37 (.in(display_driver_1_out_77));
  LED led_38 (.in(display_driver_1_out_96));
  LED led_39 (.in(display_driver_1_out_95));
  LED led_40 (.in(display_driver_1_out_90));
  LED led_41 (.in(display_driver_2_out_6));
  LED led_42 (.in(display_driver_2_out_5));
  LED led_43 (.in(display_driver_2_out_12));
  LED led_44 (.in(display_driver_2_out_18));
  LED led_45 (.in(display_driver_2_out_23));
  LED led_46 (.in(display_driver_2_out_24));
  LED led_47 (.in(display_driver_2_b));
  LED led_48 (.in(display_driver_2_a));
  LED led_49 (.in(display_driver_2_out_29));
  LED led_50 (.in(display_driver_2_c));
  LED led_51 (.in(display_driver_2_d));
  LED led_52 (.in(display_driver_2_i1));
  LED led_53 (.in(display_driver_2_out_54));
  LED led_54 (.in(display_driver_2_out_53));
  LED led_55 (.in(display_driver_2_out_60));
  LED led_56 (.in(display_driver_2_out_72));
  LED led_57 (.in(display_driver_2_out_71));
  LED led_58 (.in(display_driver_2_out_66));
  LED led_59 (.in(display_driver_2_out_78));
  LED led_60 (.in(display_driver_2_out_77));
  LED led_61 (.in(display_driver_2_out_84));
  LED led_62 (.in(display_driver_2_out_90));
  LED led_63 (.in(display_driver_2_out_95));
  LED led_64 (.in(display_driver_2_out_96));
  Button C_2 (.out(C_2_out));
  Button B_2 (.out(B_2_out));
  Button A_2 (.out(A_2_out));
  Button _0 (.out(_0_out));
  Button _2 (.out(_2_out));
  Button D (.out(D_out));
  Button _1 (.out(_1_out));
  LED led_65 (.in(display_driver_1_out_13));
  LED led_66 (.in(display_driver_1_out_7));
  LED led_67 (.in(display_driver_1_out_14));
  LED led_68 (.in(display_driver_1_out_25));
  LED led_69 (.in(display_driver_1_out_20));
  LED led_70 (.in(display_driver_1_out_19));
  LED led_71 (.in(display_driver_1_out_37));
  LED led_72 (.in(display_driver_1_out_31));
  LED led_73 (.in(display_driver_1_out_38));
  LED led_74 (.in(display_driver_1_out_44));
  LED led_75 (.in(display_driver_1_out_49));
  LED led_76 (.in(display_driver_1_out_43));
  LED led_77 (.in(display_driver_1_out_62));
  LED led_78 (.in(display_driver_1_out_55));
  LED led_79 (.in(display_driver_1_out_61));
  LED led_80 (.in(display_driver_1_out_73));
  LED led_81 (.in(display_driver_1_out_67));
  LED led_82 (.in(display_driver_1_out_68));
  LED led_83 (.in(display_driver_1_out_85));
  LED led_84 (.in(display_driver_1_out_86));
  LED led_85 (.in(display_driver_1_out_79));
  LED led_86 (.in(display_driver_1_out_92));
  LED led_87 (.in(display_driver_1_out_91));
  LED led_88 (.in(display_driver_1_out_97));
  LED led_89 (.in(display_driver_2_out_14));
  LED led_90 (.in(display_driver_2_out_13));
  LED led_91 (.in(display_driver_2_out_7));
  LED led_92 (.in(display_driver_2_out_19));
  LED led_93 (.in(display_driver_2_out_20));
  LED led_94 (.in(display_driver_2_out_25));
  LED led_95 (.in(display_driver_2_out_38));
  LED led_96 (.in(display_driver_2_out_31));
  LED led_97 (.in(display_driver_2_out_37));
  LED led_98 (.in(display_driver_2_out_44));
  LED led_99 (.in(display_driver_2_out_43));
  LED led_100 (.in(display_driver_2_out_49));
  LED led_101 (.in(display_driver_2_out_61));
  LED led_102 (.in(display_driver_2_out_55));
  LED led_103 (.in(display_driver_2_out_62));
  LED led_104 (.in(display_driver_2_out_68));
  LED led_105 (.in(display_driver_2_out_73));
  LED led_106 (.in(display_driver_2_out_67));
  LED led_107 (.in(display_driver_2_out_86));
  LED led_108 (.in(display_driver_2_out_85));
  LED led_109 (.in(display_driver_2_out_79));
  LED led_110 (.in(display_driver_2_out_92));
  LED led_111 (.in(display_driver_2_out_91));
  LED led_112 (.in(display_driver_2_out_97));
  Button _0_2 (.out(_0_2_out));
  Button D_2 (.out(D_2_out));
  Button _2_2 (.out(_2_2_out));
  Button _1_2 (.out(_1_2_out));
  Button _5 (.out(_5_out));
  Button _3 (.out(_3_out));
  Button _4 (.out(_4_out));
  LED led_113 (.in(display_driver_1_out_9));
  LED led_114 (.in(display_driver_1_out_15));
  LED led_115 (.in(display_driver_1_out_8));
  LED led_116 (.in(display_driver_1_out_26));
  LED led_117 (.in(display_driver_1_out_27));
  LED led_118 (.in(display_driver_1_out_21));
  LED led_119 (.in(display_driver_1_out_33));
  LED led_120 (.in(display_driver_1_out_32));
  LED led_121 (.in(display_driver_1_out_39));
  LED led_122 (.in(display_driver_1_out_45));
  LED led_123 (.in(display_driver_1_out_51));
  LED led_124 (.in(display_driver_1_out_50));
  LED led_125 (.in(display_driver_1_out_57));
  LED led_126 (.in(display_driver_1_out_56));
  LED led_127 (.in(display_driver_1_out_63));
  LED led_128 (.in(display_driver_1_out_69));
  LED led_129 (.in(display_driver_1_out_75));
  LED led_130 (.in(display_driver_1_out_74));
  LED led_131 (.in(display_driver_1_out_80));
  LED led_132 (.in(display_driver_1_out_81));
  LED led_133 (.in(display_driver_1_out_87));
  LED led_134 (.in(display_driver_1_out_93));
  LED led_135 (.in(display_driver_1_out_99));
  LED led_136 (.in(display_driver_1_out_98));
  LED led_137 (.in(display_driver_2_out_15));
  LED led_138 (.in(display_driver_2_out_9));
  LED led_139 (.in(display_driver_2_out_8));
  LED led_140 (.in(display_driver_2_out_27));
  LED led_141 (.in(display_driver_2_out_26));
  LED led_142 (.in(display_driver_2_out_21));
  LED led_143 (.in(display_driver_2_out_32));
  LED led_144 (.in(display_driver_2_out_33));
  LED led_145 (.in(display_driver_2_out_39));
  LED led_146 (.in(display_driver_2_out_50));
  LED led_147 (.in(display_driver_2_out_51));
  LED led_148 (.in(display_driver_2_out_45));
  LED led_149 (.in(display_driver_2_out_56));
  LED led_150 (.in(display_driver_2_out_57));
  LED led_151 (.in(display_driver_2_out_63));
  LED led_152 (.in(display_driver_2_out_69));
  LED led_153 (.in(display_driver_2_out_74));
  LED led_154 (.in(display_driver_2_out_75));
  LED led_155 (.in(display_driver_2_out_87));
  LED led_156 (.in(display_driver_2_out_81));
  LED led_157 (.in(display_driver_2_out_80));
  LED led_158 (.in(display_driver_2_out_93));
  LED led_159 (.in(display_driver_2_out_98));
  LED led_160 (.in(display_driver_2_out_99));
  Button _3_2 (.out(_3_2_out));
  Button _5_2 (.out(_5_2_out));
  Button _4_2 (.out(_4_2_out));
  Keypad keypad_1 (
    .Attack(button_out), .Attack_2(A1), .A(A_out), ._0(_0_out), .B(B_out), ._1(_1_out), .C(C_out),
    ._2(_2_out), .D(D_out), ._3(_3_out), ._4(_4_out), ._5(_5_out), .out_13(S1), .Reset(or_1_out));
  Button button (.out(button_out));
  LED led_161 (.in(display_driver_1_out_16));
  LED led_162 (.in(display_driver_1_out_10));
  Display_Driver display_driver_1 (
    .out_11(display_driver_1_out_11), .out_5(display_driver_1_out_5), .out_17(display_driver_1_out_17),
    .out_23(display_driver_1_out_23), .out_6(display_driver_1_out_6), .out_12(display_driver_1_out_12),
    .out_18(display_driver_1_out_18), .out_24(display_driver_1_out_24), .out_7(display_driver_1_out_7),
    .out_13(display_driver_1_out_13), .out_19(display_driver_1_out_19), .out_25(display_driver_1_out_25),
    .out_8(display_driver_1_out_8), .out_9(display_driver_1_out_9), .out_10(display_driver_1_out_10),
    .out_14(display_driver_1_out_14), .out_15(display_driver_1_out_15), .out_16(display_driver_1_out_16),
    .out_20(display_driver_1_out_20), .out_21(display_driver_1_out_21), .out_22(display_driver_1_out_22),
    .out_26(display_driver_1_out_26), .out_27(display_driver_1_out_27), .out_28(display_driver_1_out_28),
    .out_29(display_driver_1_out_29), .B(display_driver_1_b), .out_31(display_driver_1_out_31),
    .out_32(display_driver_1_out_32), .out_33(display_driver_1_out_33), .out_34(display_driver_1_out_34),
    .out_35(display_driver_1_out_35), .A(display_driver_1_a), .out_37(display_driver_1_out_37),
    .out_38(display_driver_1_out_38), .out_39(display_driver_1_out_39), .out_40(display_driver_1_out_40),
    .out_41(display_driver_1_out_41), .C(display_driver_1_c), .out_43(display_driver_1_out_43),
    .out_44(display_driver_1_out_44), .out_45(display_driver_1_out_45), .out_46(display_driver_1_out_46),
    .i1(display_driver_1_i1), .D(display_driver_1_d), .out_49(display_driver_1_out_49),
    .out_50(display_driver_1_out_50), .out_51(display_driver_1_out_51), .out_52(display_driver_1_out_52),
    .out_53(display_driver_1_out_53), .out_54(display_driver_1_out_54), .out_55(display_driver_1_out_55),
    .out_56(display_driver_1_out_56), .out_57(display_driver_1_out_57), .out_58(display_driver_1_out_58),
    .out_59(display_driver_1_out_59), .out_60(display_driver_1_out_60), .out_61(display_driver_1_out_61),
    .out_62(display_driver_1_out_62), .out_63(display_driver_1_out_63), .out_64(display_driver_1_out_64),
    .out_65(display_driver_1_out_65), .out_66(display_driver_1_out_66), .out_67(display_driver_1_out_67),
    .out_68(display_driver_1_out_68), .out_69(display_driver_1_out_69), .out_70(display_driver_1_out_70),
    .out_71(display_driver_1_out_71), .out_72(display_driver_1_out_72), .out_73(display_driver_1_out_73),
    .out_74(display_driver_1_out_74), .out_75(display_driver_1_out_75), .out_76(display_driver_1_out_76),
    .out_77(display_driver_1_out_77), .out_78(display_driver_1_out_78), .out_79(display_driver_1_out_79),
    .out_80(display_driver_1_out_80), .out_81(display_driver_1_out_81), .out_82(display_driver_1_out_82),
    .out_83(display_driver_1_out_83), .out_84(display_driver_1_out_84), .out_85(display_driver_1_out_85),
    .out_86(display_driver_1_out_86), .out_87(display_driver_1_out_87), .out_88(display_driver_1_out_88),
    .out_89(display_driver_1_out_89), .out_90(display_driver_1_out_90), .out_91(display_driver_1_out_91),
    .out_92(display_driver_1_out_92), .out_93(display_driver_1_out_93), .out_94(display_driver_1_out_94),
    .out_95(display_driver_1_out_95), .out_96(display_driver_1_out_96), .out_97(display_driver_1_out_97),
    .out_98(display_driver_1_out_98), .out_99(display_driver_1_out_99), .out_100(display_driver_1_out_100),
    .in_1(memory_1_d1_0), .in_2(memory_1_d1_1), .in_3(memory_1_d1_2), .in_4(memory_1_d1_3));
  LED led_163 (.in(display_driver_1_out_22));
  LED led_164 (.in(display_driver_1_out_28));
  LED led_165 (.in(display_driver_1_out_40));
  LED led_166 (.in(display_driver_1_out_34));
  LED led_167 (.in(display_driver_1_out_52));
  LED led_168 (.in(display_driver_1_out_46));
  LED led_169 (.in(display_driver_1_out_58));
  LED led_170 (.in(display_driver_1_out_64));
  LED led_171 (.in(display_driver_1_out_76));
  LED led_172 (.in(display_driver_1_out_70));
  LED led_173 (.in(display_driver_1_out_82));
  LED led_174 (.in(display_driver_1_out_88));
  LED led_175 (.in(display_driver_1_out_94));
  LED led_176 (.in(display_driver_1_out_100));
  LED led_177 (.in(display_driver_2_out_10));
  LED led_178 (.in(display_driver_2_out_16));
  Display_Driver display_driver_2 (
    .out_11(display_driver_2_out_11), .out_5(display_driver_2_out_5), .out_17(display_driver_2_out_17),
    .out_23(display_driver_2_out_23), .out_6(display_driver_2_out_6), .out_12(display_driver_2_out_12),
    .out_18(display_driver_2_out_18), .out_24(display_driver_2_out_24), .out_7(display_driver_2_out_7),
    .out_13(display_driver_2_out_13), .out_19(display_driver_2_out_19), .out_25(display_driver_2_out_25),
    .out_8(display_driver_2_out_8), .out_9(display_driver_2_out_9), .out_10(display_driver_2_out_10),
    .out_14(display_driver_2_out_14), .out_15(display_driver_2_out_15), .out_16(display_driver_2_out_16),
    .out_20(display_driver_2_out_20), .out_21(display_driver_2_out_21), .out_22(display_driver_2_out_22),
    .out_26(display_driver_2_out_26), .out_27(display_driver_2_out_27), .out_28(display_driver_2_out_28),
    .out_29(display_driver_2_out_29), .B(display_driver_2_b), .out_31(display_driver_2_out_31),
    .out_32(display_driver_2_out_32), .out_33(display_driver_2_out_33), .out_34(display_driver_2_out_34),
    .out_35(display_driver_2_out_35), .A(display_driver_2_a), .out_37(display_driver_2_out_37),
    .out_38(display_driver_2_out_38), .out_39(display_driver_2_out_39), .out_40(display_driver_2_out_40),
    .out_41(display_driver_2_out_41), .C(display_driver_2_c), .out_43(display_driver_2_out_43),
    .out_44(display_driver_2_out_44), .out_45(display_driver_2_out_45), .out_46(display_driver_2_out_46),
    .i1(display_driver_2_i1), .D(display_driver_2_d), .out_49(display_driver_2_out_49),
    .out_50(display_driver_2_out_50), .out_51(display_driver_2_out_51), .out_52(display_driver_2_out_52),
    .out_53(display_driver_2_out_53), .out_54(display_driver_2_out_54), .out_55(display_driver_2_out_55),
    .out_56(display_driver_2_out_56), .out_57(display_driver_2_out_57), .out_58(display_driver_2_out_58),
    .out_59(display_driver_2_out_59), .out_60(display_driver_2_out_60), .out_61(display_driver_2_out_61),
    .out_62(display_driver_2_out_62), .out_63(display_driver_2_out_63), .out_64(display_driver_2_out_64),
    .out_65(display_driver_2_out_65), .out_66(display_driver_2_out_66), .out_67(display_driver_2_out_67),
    .out_68(display_driver_2_out_68), .out_69(display_driver_2_out_69), .out_70(display_driver_2_out_70),
    .out_71(display_driver_2_out_71), .out_72(display_driver_2_out_72), .out_73(display_driver_2_out_73),
    .out_74(display_driver_2_out_74), .out_75(display_driver_2_out_75), .out_76(display_driver_2_out_76),
    .out_77(display_driver_2_out_77), .out_78(display_driver_2_out_78), .out_79(display_driver_2_out_79),
    .out_80(display_driver_2_out_80), .out_81(display_driver_2_out_81), .out_82(display_driver_2_out_82),
    .out_83(display_driver_2_out_83), .out_84(display_driver_2_out_84), .out_85(display_driver_2_out_85),
    .out_86(display_driver_2_out_86), .out_87(display_driver_2_out_87), .out_88(display_driver_2_out_88),
    .out_89(display_driver_2_out_89), .out_90(display_driver_2_out_90), .out_91(display_driver_2_out_91),
    .out_92(display_driver_2_out_92), .out_93(display_driver_2_out_93), .out_94(display_driver_2_out_94),
    .out_95(display_driver_2_out_95), .out_96(display_driver_2_out_96), .out_97(display_driver_2_out_97),
    .out_98(display_driver_2_out_98), .out_99(display_driver_2_out_99), .out_100(display_driver_2_out_100),
    .in_1(memory_1_d2_0), .in_2(memory_1_d2_1), .in_3(memory_1_d2_2), .in_4(memory_1_d2_3));
  LED led_179 (.in(display_driver_2_out_28));
  LED led_180 (.in(display_driver_2_out_22));
  LED led_181 (.in(display_driver_2_out_34));
  LED led_182 (.in(display_driver_2_out_40));
  LED led_183 (.in(display_driver_2_out_46));
  LED led_184 (.in(display_driver_2_out_52));
  LED led_185 (.in(display_driver_2_out_58));
  LED led_186 (.in(display_driver_2_out_64));
  LED led_187 (.in(display_driver_2_out_76));
  LED led_188 (.in(display_driver_2_out_70));
  LED led_189 (.in(display_driver_2_out_88));
  LED led_190 (.in(display_driver_2_out_82));
  LED led_191 (.in(display_driver_2_out_100));
  LED led_192 (.in(display_driver_2_out_94));
  Button button_2 (.out(button_2_out));
  Keypad keypad_2 (
    .Attack(button_2_out), .Attack_2(A2), .A(A_2_out), ._0(_0_2_out), .B(B_2_out), ._1(_1_2_out),
    .C(C_2_out), ._2(_2_2_out), .D(D_2_out), ._3(_3_2_out), ._4(_4_2_out), ._5(_5_2_out), .out_13(S2),
    .Reset(or_2_out));
  LED Your_Turn (.in(and_2_out));
  and and_2 (and_2_out, ~Win, ~StateOut[1]);  // AND_Gate
  Hex_Digit_Display hex_digit_display_1 (.value(s_c_displaydriver_1_out));  // open: dp
  S_C_DisplayDriver s_c_displaydriver_1 (.State(S_C_1), .Out(s_c_displaydriver_1_out));
  LED Your_Turn_2 (.in(and_3_out));
  and and_3 (and_3_out, ~Win, StateOut[1]);  // AND_Gate
  Hex_Digit_Display hex_digit_display_2 (.value(s_c_displaydriver_2_out));  // open: dp
  S_C_DisplayDriver s_c_displaydriver_2 (.State(S_C_2), .Out(s_c_displaydriver_2_out));
  Button New_Game (.out(Reset));

  // Notes on the sheet:
  //   A
  //   B
  //   C
  //   D
  //   A
  //   B
  //   C
  //   D
  //   1 
  //   0
  //   3 
  //   2 
  //   4 
  //   Your Ship
  //   5 
  //   Your Ship
endmodule

module Display_Driver (
  input  [11:0] in_1,
  input  [11:0] in_2,
  input  [11:0] in_3,
  input  [11:0] in_4,
  output out_5,
  output out_6,
  output out_7,
  output out_8,
  output out_9,
  output out_10,
  output out_11,
  output out_12,
  output out_13,
  output out_14,
  output out_15,
  output out_16,
  output out_17,
  output out_18,
  output out_19,
  output out_20,
  output out_21,
  output out_22,
  output out_23,
  output out_24,
  output out_25,
  output out_26,
  output out_27,
  output out_28,
  output out_29,
  output B,
  output out_31,
  output out_32,
  output out_33,
  output out_34,
  output out_35,
  output A,
  output out_37,
  output out_38,
  output out_39,
  output out_40,
  output out_41,
  output C,
  output out_43,
  output out_44,
  output out_45,
  output out_46,
  output i1,
  output D,
  output out_49,
  output out_50,
  output out_51,
  output out_52,
  output out_53,
  output out_54,
  output out_55,
  output out_56,
  output out_57,
  output out_58,
  output out_59,
  output out_60,
  output out_61,
  output out_62,
  output out_63,
  output out_64,
  output out_65,
  output out_66,
  output out_67,
  output out_68,
  output out_69,
  output out_70,
  output out_71,
  output out_72,
  output out_73,
  output out_74,
  output out_75,
  output out_76,
  output out_77,
  output out_78,
  output out_79,
  output out_80,
  output out_81,
  output out_82,
  output out_83,
  output out_84,
  output out_85,
  output out_86,
  output out_87,
  output out_88,
  output out_89,
  output out_90,
  output out_91,
  output out_92,
  output out_93,
  output out_94,
  output out_95,
  output out_96,
  output out_97,
  output out_98,
  output out_99,
  output out_100
);

  xor xor_1 (out_11, in_1[11], in_1[10]);
  xor xor_2 (i1, in_2[11], in_2[10]);
  xor xor_3 (out_59, in_3[11], in_3[10]);
  xor xor_4 (out_83, in_4[11], in_4[10]);
  xor xor_5 (out_12, in_1[9], in_1[8]);
  xor xor_6 (A, in_2[9], in_2[8]);
  xor xor_7 (out_60, in_3[9], in_3[8]);
  xor xor_8 (out_84, in_4[9], in_4[8]);
  xor xor_9 (out_13, in_1[7], in_1[6]);
  xor xor_10 (out_37, in_2[7], in_2[6]);
  xor xor_11 (out_61, in_3[7], in_3[6]);
  xor xor_12 (out_85, in_4[7], in_4[6]);
  xor xor_13 (out_14, in_1[5], in_1[4]);
  xor xor_14 (out_38, in_2[5], in_2[4]);
  xor xor_15 (out_62, in_3[5], in_3[4]);
  xor xor_16 (out_86, in_4[5], in_4[4]);
  xor xor_17 (out_15, in_1[3], in_1[2]);
  xor xor_18 (out_39, in_2[3], in_2[2]);
  xor xor_19 (out_63, in_3[3], in_3[2]);
  xor xor_20 (out_87, in_4[3], in_4[2]);
  xor xor_21 (out_16, in_1[1], in_1[0]);
  xor xor_22 (out_40, in_2[1], in_2[0]);
  xor xor_23 (out_64, in_3[1], in_3[0]);
  xor xor_24 (out_88, in_4[1], in_4[0]);

  assign B = in_2[8];
  assign C = in_2[8];
  assign D = A;
  assign out_5 = in_1[10];
  assign out_6 = in_1[8];
  assign out_7 = in_1[6];
  assign out_8 = in_1[4];
  assign out_9 = in_1[2];
  assign out_10 = in_1[0];
  assign out_17 = in_1[10];
  assign out_18 = in_1[8];
  assign out_19 = in_1[6];
  assign out_20 = in_1[4];
  assign out_21 = in_1[2];
  assign out_22 = in_1[0];
  assign out_23 = out_11;
  assign out_24 = out_12;
  assign out_25 = out_13;
  assign out_26 = out_14;
  assign out_27 = out_15;
  assign out_28 = out_16;
  assign out_29 = in_2[10];
  assign out_31 = in_2[6];
  assign out_32 = in_2[4];
  assign out_33 = in_2[2];
  assign out_34 = in_2[0];
  assign out_35 = i1;
  assign out_41 = in_2[10];
  assign out_43 = in_2[6];
  assign out_44 = in_2[4];
  assign out_45 = in_2[2];
  assign out_46 = in_2[0];
  assign out_49 = out_37;
  assign out_50 = out_38;
  assign out_51 = out_39;
  assign out_52 = out_40;
  assign out_53 = in_3[10];
  assign out_54 = in_3[8];
  assign out_55 = in_3[6];
  assign out_56 = in_3[4];
  assign out_57 = in_3[2];
  assign out_58 = in_3[0];
  assign out_65 = in_3[10];
  assign out_66 = in_3[8];
  assign out_67 = in_3[6];
  assign out_68 = in_3[4];
  assign out_69 = in_3[2];
  assign out_70 = in_3[0];
  assign out_71 = out_59;
  assign out_72 = out_60;
  assign out_73 = out_61;
  assign out_74 = out_62;
  assign out_75 = out_63;
  assign out_76 = out_64;
  assign out_77 = in_4[10];
  assign out_78 = in_4[8];
  assign out_79 = in_4[6];
  assign out_80 = in_4[4];
  assign out_81 = in_4[2];
  assign out_82 = in_4[0];
  assign out_89 = in_4[10];
  assign out_90 = in_4[8];
  assign out_91 = in_4[6];
  assign out_92 = in_4[4];
  assign out_93 = in_4[2];
  assign out_94 = in_4[0];
  assign out_95 = out_83;
  assign out_96 = out_84;
  assign out_97 = out_85;
  assign out_98 = out_86;
  assign out_99 = out_87;
  assign out_100 = out_88;

  // Notes on the sheet:
  //   i2
endmodule

module AttackProcessor (
  input  [1:0] ValueIn,
  input  [2:0] State,
  output [1:0] ValueOut
);

  wire and_1_out, and_2_out, and_3_out, and_4_out, or_1_out;

  and and_1 (and_1_out, ~State[2], State[0]);  // AND_Gate
  and and_2 (and_2_out, ValueIn[0], ~State[0]);  // AND_Gate
  and and_3 (and_3_out, State[0], State[2], ValueIn[0]);
  and and_4 (and_4_out, ~ValueIn[0], ValueIn[1]);  // AND_Gate
  or or_1 (or_1_out, and_1_out, and_2_out);
  or or_2 (ValueOut[1], and_3_out, and_4_out);
  and and_5 (ValueOut[0], ~ValueIn[1], or_1_out);  // AND_Gate
endmodule

module ShipCountManager (
  input  [1:0] Current_value,
  input  [1:0] Attack_Proc_or_Out,
  input  [2:0] State,
  input  [2:0] ShipCount1,
  input  [2:0] ShipCount2,
  output Player,
  output [2:0] Out
);

  wire xor_1_out, xor_2_out, xor_4_out;
  wire [3:0] and_2_out, and_3_out, and_4_out, and_5_out, or_2_out;
  wire [3:3] adder_4bit_1_result, not_1_out, not_2_out, or_1_out;

  xor xor_1 (xor_1_out, Current_value[0], Attack_Proc_or_Out[0]);
  xor xor_2 (xor_2_out, Current_value[1], Attack_Proc_or_Out[1]);
  or or_1 (or_1_out[3], xor_1_out, xor_2_out);
  xor xor_3 (Player, State[1], State[2]);
  not not_1 (not_1_out[3], 1'b1);
  not not_2 (not_2_out[3], 1'b1);
  and and_1 (and_4_out[3], ~Attack_Proc_or_Out[0], Attack_Proc_or_Out[1], State[0], State[2]);  // AND_Gate
  xor xor_4 (xor_4_out, Attack_Proc_or_Out[0], Attack_Proc_or_Out[1]);
  assign and_2_out = ~{4{Player}} & {not_1_out[3], ShipCount1};  // AND_Gate and_2, 4 bits wide
  assign and_3_out = {4{Player}} & {not_2_out[3], ShipCount2};  // AND_Gate and_3, 4 bits wide
  and and_4 (and_4_out[0], State[0], xor_4_out);
  assign and_5_out = {4{or_1_out[3]}} & {{3{and_4_out[3]}}, and_4_out[0]};  // AND_Gate and_5, 4 bits wide
  assign or_2_out = and_2_out | and_3_out;  // OR_Gate or_2, 4 bits wide
  Adder_4bit adder_4bit_1 (.a(and_5_out), .b(or_2_out), .Result({adder_4bit_1_result[3], Out}));
endmodule

module Keypad (
  input  A,
  input  B,
  input  C,
  input  D,
  input  _0,
  input  _1,
  input  _2,
  input  _3,
  input  _4,
  input  _5,
  input  Reset,
  input  Attack,
  output [4:0] out_13,
  output Attack_2
);

  wire _00, _01, _02, _10, _11, _12, _20, _21, _22, _30, _31, _32, _40, _41, _42, _50, _51, _52, A0, A1, B0,
       B1, C0, C1, D0, D1, nor_1_out, not_1_out, not_2_out, not_3_out, not_4_out, not_5_out, not_6_out,
       not_7_out, not_8_out, not_9_out, not_10_out, not_11_out, not_12_out, not_13_out, not_14_out,
       not_15_out, or_1_out, or_2_out, or_4_out, or_5_out, or_6_out;
  wire [1:0] and_8_out, or_7_out;
  wire [2:0] and_16_out, or_10_out;

  not not_1 (not_1_out, A);
  not not_2 (not_2_out, A);
  and and_1 (A0, A, not_1_out);
  and and_2 (A1, A, not_2_out);
  or or_1 (or_1_out, A, B, C, D);
  not not_3 (not_3_out, _0);
  not not_4 (not_4_out, _0);
  not not_5 (not_5_out, _0);
  and and_3 (_01, _0, not_4_out);
  and and_4 (_02, _0, not_5_out);
  or or_2 (or_2_out, _0, _1, _2, _3, _4, _5);
  not not_6 (not_6_out, B);
  and and_5 (B1, B, not_6_out);
  or or_3 (or_7_out[1], A1, B1, C1, D1);
  and and_6 (_00, _0, not_3_out);
  nor nor_1 (nor_1_out, Reset, ~Attack);  // NOR_Gate
  or or_4 (or_4_out, Reset, Attack);
  and and_7 (B0, B, B);
  assign and_8_out = or_7_out & ~{2{Reset}};  // AND_Gate and_8, 2 bits wide
  or or_5 (or_5_out, Reset, or_1_out);
  not not_7 (not_7_out, _1);
  not not_8 (not_8_out, _1);
  and and_9 (_12, _1, not_8_out);
  or or_6 (or_6_out, Reset, or_2_out);
  not not_9 (not_9_out, C);
  and and_10 (C0, C, not_9_out);
  and and_11 (C1, C, C);
  or or_7 (or_7_out[0], A0, B0, C0, D0);
  and and_12 (_11, _1, not_7_out);
  and and_13 (_10, _1, _1);
  or or_8 (or_10_out[2], _02, _12, _22, _32, _42, _52);
  and and_14 (D1, D, D);
  Register_2Bit register_2bit_1 (.IN(and_8_out), .Clock(or_5_out), .Q(out_13[4:3]));
  not not_10 (not_10_out, _2);
  not not_11 (not_11_out, _2);
  and and_15 (_22, _2, not_11_out);
  assign and_16_out = or_10_out & ~{3{Reset}};  // AND_Gate and_16, 3 bits wide
  and and_17 (D0, D, D);
  and and_18 (_21, _2, _2);
  and and_19 (_20, _2, not_10_out);
  or or_9 (or_10_out[1], _01, _11, _21, _31, _41, _51);
  FlipFlopDT flipflopdt_1 (.D(nor_1_out), .Clock(or_4_out), .Q(Attack_2));  // open: nQ
  not not_12 (not_12_out, _3);
  and and_20 (_32, _3, not_12_out);
  Register_3Bit register_3bit_1 (.IN(and_16_out), .Clock(or_6_out), .OUT(out_13[2:0]));
  and and_21 (_31, _3, _3);
  and and_22 (_30, _3, _3);
  or or_10 (or_10_out[0], _00, _10, _20, _30, _40, _50);
  not not_13 (not_13_out, _4);
  not not_14 (not_14_out, _4);
  and and_23 (_42, _4, _4);
  and and_24 (_41, _4, not_14_out);
  and and_25 (_40, _4, not_13_out);
  not not_15 (not_15_out, _5);
  and and_26 (_51, _5, not_15_out);
  and and_27 (_52, _5, _5);
  and and_28 (_50, _5, _5);

  // Other names for the same wires on the sheet: Row[1:0] = out_13[4:3]
endmodule

module Memory (
  input  [5:0] Register,
  input  Clock,
  input  Reset,
  input  [1:0] Write_content,
  input  [2:0] State_write,
  input  B_C__Player_write,
  input  [2:0] Write_boat_count,
  output [11:0] D2_3,
  output [11:0] D2_2,
  output [11:0] D2_1,
  output [11:0] D2_0,
  output [11:0] D1_3,
  output [11:0] D1_2,
  output [11:0] D1_1,
  output [11:0] D1_0,
  output [1:0] Read_out,
  output [2:0] State_out,
  output [2:0] B_C__1_out,
  output [2:0] B_C__2_out
);

  wire and_3_out, and_4_out, and_5_out, and_6_out, and_7_out, and_8_out, and_9_out, and_10_out, and_11_out,
       and_12_out, and_13_out, and_14_out, and_15_out, and_16_out, and_17_out, and_18_out, and_19_out,
       and_20_out, and_21_out, and_22_out, and_23_out, and_24_out, and_25_out, and_26_out, and_27_out,
       and_28_out, and_29_out, and_30_out, and_31_out, and_32_out, and_33_out, and_34_out, and_35_out,
       and_36_out, and_37_out, and_38_out, and_39_out, and_40_out, and_41_out, and_42_out, and_43_out,
       and_44_out, and_45_out, and_46_out, and_47_out, and_48_out, and_49_out, and_50_out, and_51_out,
       and_52_out, and_53_out, and_54_out, and_55_out, and_56_out, and_57_out, and_58_out, and_59_out,
       and_60_out, and_61_out, and_62_out, and_63_out, and_64_out, and_65_out, and_66_out, and_67_out,
       and_68_out, decoder_1_out_2, decoder_1_out_3, decoder_1_out_4, decoder_1_out_5, decoder_1_out_6,
       decoder_1_out_7, decoder_1_out_8, decoder_1_out_9, decoder_1_out_10, decoder_1_out_11,
       decoder_1_out_12, decoder_1_out_13, decoder_1_out_14, decoder_1_out_15, decoder_1_out_16,
       decoder_1_out_17, decoder_1_out_18, decoder_1_out_19, decoder_1_out_20, decoder_1_out_21,
       decoder_1_out_22, decoder_1_out_23, decoder_1_out_24, decoder_1_out_25, decoder_1_out_26,
       decoder_1_out_27, decoder_1_out_28, decoder_1_out_29, decoder_1_out_30, decoder_1_out_31,
       decoder_1_out_32, decoder_1_out_33, decoder_1_out_34, decoder_1_out_35, decoder_1_out_36,
       decoder_1_out_37, decoder_1_out_38, decoder_1_out_39, decoder_1_out_40, decoder_1_out_41,
       decoder_1_out_42, decoder_1_out_43, decoder_1_out_44, decoder_1_out_45, decoder_1_out_46,
       decoder_1_out_47, decoder_1_out_48, decoder_1_out_49, decoder_1_out_50, decoder_1_out_51,
       decoder_1_out_52, decoder_1_out_53, decoder_1_out_54, decoder_1_out_55, decoder_1_out_56,
       decoder_1_out_57, decoder_1_out_58, decoder_1_out_59, decoder_1_out_60, decoder_1_out_61,
       decoder_1_out_62, decoder_1_out_63, decoder_1_out_64, decoder_1_out_65, or_1_out, or_2_out, or_3_out,
       or_4_out, or_5_out, or_6_out, or_7_out, or_8_out, or_9_out, or_10_out, or_11_out, or_12_out,
       or_13_out, or_14_out, or_15_out, or_16_out, or_17_out, or_18_out, or_19_out, or_20_out, or_21_out,
       or_22_out, or_23_out, or_24_out, or_25_out, or_26_out, or_27_out, or_28_out, or_29_out, or_30_out,
       or_31_out, or_32_out, or_33_out, or_34_out, or_35_out, or_36_out, or_37_out, or_38_out, or_39_out,
       or_40_out, or_41_out, or_42_out, or_43_out, or_44_out, or_45_out, or_46_out, or_47_out, or_48_out,
       or_49_out, or_50_out, or_51_out, or_52_out, or_53_out, or_54_out, or_55_out, or_56_out, or_57_out,
       or_58_out, or_59_out, or_60_out, or_61_out, or_62_out, or_63_out, or_64_out, or_65_out, or_66_out,
       or_67_out;
  wire [1:0] and_69_out, register_2bit_1_q, register_2bit_2_q, register_2bit_9_q, register_2bit_10_q,
       register_2bit_17_q, register_2bit_18_q, register_2bit_25_q, register_2bit_26_q, register_2bit_33_q,
       register_2bit_34_q, register_2bit_41_q, register_2bit_42_q, register_2bit_49_q, register_2bit_50_q,
       register_2bit_57_q, register_2bit_58_q;
  wire [2:0] and_1_out, and_2_out;

  assign and_1_out = ~{3{Reset}} & State_write;  // AND_Gate and_1, 3 bits wide
  assign and_2_out = ~{3{Reset}} & Write_boat_count;  // AND_Gate and_2, 3 bits wide
  Decoder decoder_1 (
    .in_1(Register), .out_2(decoder_1_out_2), .out_3(decoder_1_out_3), .out_4(decoder_1_out_4),
    .out_5(decoder_1_out_5), .out_6(decoder_1_out_6), .out_7(decoder_1_out_7), .out_8(decoder_1_out_8),
    .out_9(decoder_1_out_9), .out_10(decoder_1_out_10), .out_11(decoder_1_out_11), .out_12(decoder_1_out_12),
    .out_13(decoder_1_out_13), .out_14(decoder_1_out_14), .out_15(decoder_1_out_15),
    .out_16(decoder_1_out_16), .out_17(decoder_1_out_17), .out_18(decoder_1_out_18),
    .out_19(decoder_1_out_19), .out_20(decoder_1_out_20), .out_21(decoder_1_out_21),
    .out_22(decoder_1_out_22), .out_23(decoder_1_out_23), .out_24(decoder_1_out_24),
    .out_25(decoder_1_out_25), .out_26(decoder_1_out_26), .out_27(decoder_1_out_27),
    .out_28(decoder_1_out_28), .out_29(decoder_1_out_29), .out_30(decoder_1_out_30),
    .out_31(decoder_1_out_31), .out_32(decoder_1_out_32), .out_33(decoder_1_out_33),
    .out_34(decoder_1_out_34), .out_35(decoder_1_out_35), .out_36(decoder_1_out_36),
    .out_37(decoder_1_out_37), .out_38(decoder_1_out_38), .out_39(decoder_1_out_39),
    .out_40(decoder_1_out_40), .out_41(decoder_1_out_41), .out_42(decoder_1_out_42),
    .out_43(decoder_1_out_43), .out_44(decoder_1_out_44), .out_45(decoder_1_out_45),
    .out_46(decoder_1_out_46), .out_47(decoder_1_out_47), .out_48(decoder_1_out_48),
    .out_49(decoder_1_out_49), .out_50(decoder_1_out_50), .out_51(decoder_1_out_51),
    .out_52(decoder_1_out_52), .out_53(decoder_1_out_53), .out_54(decoder_1_out_54),
    .out_55(decoder_1_out_55), .out_56(decoder_1_out_56), .out_57(decoder_1_out_57),
    .out_58(decoder_1_out_58), .out_59(decoder_1_out_59), .out_60(decoder_1_out_60),
    .out_61(decoder_1_out_61), .out_62(decoder_1_out_62), .out_63(decoder_1_out_63),
    .out_64(decoder_1_out_64), .out_65(decoder_1_out_65));
  and and_3 (and_3_out, decoder_1_out_65, Clock);
  and and_4 (and_4_out, decoder_1_out_64, Clock);
  and and_5 (and_5_out, decoder_1_out_63, Clock);
  and and_6 (and_6_out, decoder_1_out_62, Clock);
  and and_7 (and_7_out, decoder_1_out_61, Clock);
  and and_8 (and_8_out, decoder_1_out_60, Clock);
  and and_9 (and_9_out, decoder_1_out_59, Clock);
  and and_10 (and_10_out, decoder_1_out_58, Clock);
  and and_11 (and_11_out, decoder_1_out_57, Clock);
  and and_12 (and_12_out, decoder_1_out_56, Clock);
  and and_13 (and_13_out, decoder_1_out_55, Clock);
  and and_14 (and_14_out, decoder_1_out_54, Clock);
  and and_15 (and_15_out, decoder_1_out_53, Clock);
  and and_16 (and_16_out, decoder_1_out_52, Clock);
  and and_17 (and_17_out, decoder_1_out_51, Clock);
  and and_18 (and_18_out, decoder_1_out_50, Clock);
  and and_19 (and_19_out, decoder_1_out_49, Clock);
  and and_20 (and_20_out, decoder_1_out_48, Clock);
  and and_21 (and_21_out, decoder_1_out_47, Clock);
  and and_22 (and_22_out, decoder_1_out_46, Clock);
  and and_23 (and_23_out, decoder_1_out_45, Clock);
  and and_24 (and_24_out, decoder_1_out_44, Clock);
  and and_25 (and_25_out, decoder_1_out_43, Clock);
  and and_26 (and_26_out, decoder_1_out_42, Clock);
  and and_27 (and_27_out, decoder_1_out_41, Clock);
  and and_28 (and_28_out, decoder_1_out_40, Clock);
  and and_29 (and_29_out, decoder_1_out_39, Clock);
  and and_30 (and_30_out, decoder_1_out_38, Clock);
  and and_31 (and_31_out, decoder_1_out_37, Clock);
  and and_32 (and_32_out, decoder_1_out_36, Clock);
  and and_33 (and_33_out, decoder_1_out_35, Clock);
  and and_34 (and_34_out, decoder_1_out_34, Clock);
  and and_35 (and_35_out, decoder_1_out_33, Clock);
  and and_36 (and_36_out, decoder_1_out_32, Clock);
  and and_37 (and_37_out, decoder_1_out_31, Clock);
  and and_38 (and_38_out, decoder_1_out_30, Clock);
  and and_39 (and_39_out, decoder_1_out_29, Clock);
  and and_40 (and_40_out, decoder_1_out_28, Clock);
  and and_41 (and_41_out, decoder_1_out_27, Clock);
  and and_42 (and_42_out, decoder_1_out_26, Clock);
  and and_43 (and_43_out, decoder_1_out_25, Clock);
  and and_44 (and_44_out, decoder_1_out_24, Clock);
  and and_45 (and_45_out, decoder_1_out_23, Clock);
  and and_46 (and_46_out, decoder_1_out_22, Clock);
  and and_47 (and_47_out, decoder_1_out_21, Clock);
  and and_48 (and_48_out, decoder_1_out_20, Clock);
  and and_49 (and_49_out, decoder_1_out_19, Clock);
  and and_50 (and_50_out, decoder_1_out_18, Clock);
  and and_51 (and_51_out, decoder_1_out_17, Clock);
  and and_52 (and_52_out, decoder_1_out_16, Clock);
  and and_53 (and_53_out, decoder_1_out_15, Clock);
  and and_54 (and_54_out, decoder_1_out_14, Clock);
  and and_55 (and_55_out, decoder_1_out_13, Clock);
  and and_56 (and_56_out, decoder_1_out_12, Clock);
  and and_57 (and_57_out, decoder_1_out_11, Clock);
  and and_58 (and_58_out, decoder_1_out_10, Clock);
  and and_59 (and_59_out, decoder_1_out_9, Clock);
  and and_60 (and_60_out, decoder_1_out_8, Clock);
  and and_61 (and_61_out, decoder_1_out_7, Clock);
  and and_62 (and_62_out, decoder_1_out_6, Clock);
  and and_63 (and_63_out, decoder_1_out_5, Clock);
  and and_64 (and_64_out, decoder_1_out_4, Clock);
  and and_65 (and_65_out, decoder_1_out_3, Clock);
  and and_66 (and_66_out, decoder_1_out_2, Clock);
  and and_67 (and_67_out, ~B_C__Player_write, Clock);  // AND_Gate
  and and_68 (and_68_out, B_C__Player_write, Clock);
  or or_1 (or_1_out, and_3_out, Reset);
  or or_2 (or_2_out, and_4_out, Reset);
  or or_3 (or_3_out, and_5_out, Reset);
  or or_4 (or_4_out, and_6_out, Reset);
  or or_5 (or_5_out, and_7_out, Reset);
  or or_6 (or_6_out, and_8_out, Reset);
  or or_7 (or_7_out, and_9_out, Reset);
  or or_8 (or_8_out, and_10_out, Reset);
  or or_9 (or_9_out, and_11_out, Reset);
  or or_10 (or_10_out, and_12_out, Reset);
  or or_11 (or_11_out, and_13_out, Reset);
  or or_12 (or_12_out, and_14_out, Reset);
  or or_13 (or_13_out, and_15_out, Reset);
  or or_14 (or_14_out, and_16_out, Reset);
  or or_15 (or_15_out, and_17_out, Reset);
  or or_16 (or_16_out, and_18_out, Reset);
  or or_17 (or_17_out, and_19_out, Reset);
  or or_18 (or_18_out, and_20_out, Reset);
  or or_19 (or_19_out, and_21_out, Reset);
  or or_20 (or_20_out, and_22_out, Reset);
  or or_21 (or_21_out, and_23_out, Reset);
  or or_22 (or_22_out, and_24_out, Reset);
  or or_23 (or_23_out, and_25_out, Reset);
  or or_24 (or_24_out, and_26_out, Reset);
  or or_25 (or_25_out, and_27_out, Reset);
  or or_26 (or_26_out, and_28_out, Reset);
  or or_27 (or_27_out, and_29_out, Reset);
  or or_28 (or_28_out, and_30_out, Reset);
  or or_29 (or_29_out, and_31_out, Reset);
  or or_30 (or_30_out, and_32_out, Reset);
  or or_31 (or_31_out, and_33_out, Reset);
  or or_32 (or_32_out, and_34_out, Reset);
  or or_33 (or_33_out, and_35_out, Reset);
  or or_34 (or_34_out, and_36_out, Reset);
  or or_35 (or_35_out, and_37_out, Reset);
  or or_36 (or_36_out, and_38_out, Reset);
  or or_37 (or_37_out, and_39_out, Reset);
  or or_38 (or_38_out, and_40_out, Reset);
  or or_39 (or_39_out, and_41_out, Reset);
  or or_40 (or_40_out, and_42_out, Reset);
  or or_41 (or_41_out, and_43_out, Reset);
  or or_42 (or_42_out, and_44_out, Reset);
  or or_43 (or_43_out, and_45_out, Reset);
  or or_44 (or_44_out, and_46_out, Reset);
  or or_45 (or_45_out, and_47_out, Reset);
  or or_46 (or_46_out, and_48_out, Reset);
  or or_47 (or_47_out, and_49_out, Reset);
  or or_48 (or_48_out, and_50_out, Reset);
  or or_49 (or_49_out, and_51_out, Reset);
  or or_50 (or_50_out, and_52_out, Reset);
  or or_51 (or_51_out, and_53_out, Reset);
  or or_52 (or_52_out, and_54_out, Reset);
  or or_53 (or_53_out, and_55_out, Reset);
  or or_54 (or_54_out, and_56_out, Reset);
  or or_55 (or_55_out, and_57_out, Reset);
  or or_56 (or_56_out, and_58_out, Reset);
  or or_57 (or_57_out, and_59_out, Reset);
  or or_58 (or_58_out, and_60_out, Reset);
  or or_59 (or_59_out, and_61_out, Reset);
  or or_60 (or_60_out, and_62_out, Reset);
  or or_61 (or_61_out, and_63_out, Reset);
  or or_62 (or_62_out, and_64_out, Reset);
  or or_63 (or_63_out, and_65_out, Reset);
  or or_64 (or_64_out, and_66_out, Reset);
  or or_65 (or_65_out, Clock, Reset);
  or or_66 (or_66_out, and_67_out, Reset);
  or or_67 (or_67_out, and_68_out, Reset);
  assign and_69_out = ~{2{Reset}} & Write_content;  // AND_Gate and_69, 2 bits wide
  Register_2Bit register_2bit_1 (.IN(and_69_out), .Clock(or_1_out), .Q(register_2bit_1_q));
  Register_2Bit register_2bit_2 (.IN(and_69_out), .Clock(or_2_out), .Q(register_2bit_2_q));
  Register_2Bit register_2bit_3 (.IN(and_69_out), .Clock(or_3_out), .Q(D2_3[1:0]));
  Register_2Bit register_2bit_4 (.IN(and_69_out), .Clock(or_4_out), .Q(D2_3[3:2]));
  Register_2Bit register_2bit_5 (.IN(and_69_out), .Clock(or_5_out), .Q(D2_3[5:4]));
  Register_2Bit register_2bit_6 (.IN(and_69_out), .Clock(or_6_out), .Q(D2_3[7:6]));
  Register_2Bit register_2bit_7 (.IN(and_69_out), .Clock(or_7_out), .Q(D2_3[9:8]));
  Register_2Bit register_2bit_8 (.IN(and_69_out), .Clock(or_8_out), .Q(D2_3[11:10]));
  Register_2Bit register_2bit_9 (.IN(and_69_out), .Clock(or_9_out), .Q(register_2bit_9_q));
  Register_2Bit register_2bit_10 (.IN(and_69_out), .Clock(or_10_out), .Q(register_2bit_10_q));
  Register_2Bit register_2bit_11 (.IN(and_69_out), .Clock(or_11_out), .Q(D2_2[1:0]));
  Register_2Bit register_2bit_12 (.IN(and_69_out), .Clock(or_12_out), .Q(D2_2[3:2]));
  Register_2Bit register_2bit_13 (.IN(and_69_out), .Clock(or_13_out), .Q(D2_2[5:4]));
  Register_2Bit register_2bit_14 (.IN(and_69_out), .Clock(or_14_out), .Q(D2_2[7:6]));
  Register_2Bit register_2bit_15 (.IN(and_69_out), .Clock(or_15_out), .Q(D2_2[9:8]));
  Register_2Bit register_2bit_16 (.IN(and_69_out), .Clock(or_16_out), .Q(D2_2[11:10]));
  Register_2Bit register_2bit_17 (.IN(and_69_out), .Clock(or_17_out), .Q(register_2bit_17_q));
  Register_2Bit register_2bit_18 (.IN(and_69_out), .Clock(or_18_out), .Q(register_2bit_18_q));
  Register_2Bit register_2bit_19 (.IN(and_69_out), .Clock(or_19_out), .Q(D2_1[1:0]));
  Register_2Bit register_2bit_20 (.IN(and_69_out), .Clock(or_20_out), .Q(D2_1[3:2]));
  Register_2Bit register_2bit_21 (.IN(and_69_out), .Clock(or_21_out), .Q(D2_1[5:4]));
  Register_2Bit register_2bit_22 (.IN(and_69_out), .Clock(or_22_out), .Q(D2_1[7:6]));
  Register_2Bit register_2bit_23 (.IN(and_69_out), .Clock(or_23_out), .Q(D2_1[9:8]));
  Register_2Bit register_2bit_24 (.IN(and_69_out), .Clock(or_24_out), .Q(D2_1[11:10]));
  Register_2Bit register_2bit_25 (.IN(and_69_out), .Clock(or_25_out), .Q(register_2bit_25_q));
  Register_2Bit register_2bit_26 (.IN(and_69_out), .Clock(or_26_out), .Q(register_2bit_26_q));
  Register_2Bit register_2bit_27 (.IN(and_69_out), .Clock(or_27_out), .Q(D2_0[1:0]));
  Register_2Bit register_2bit_28 (.IN(and_69_out), .Clock(or_28_out), .Q(D2_0[3:2]));
  Register_2Bit register_2bit_29 (.IN(and_69_out), .Clock(or_29_out), .Q(D2_0[5:4]));
  Register_2Bit register_2bit_30 (.IN(and_69_out), .Clock(or_30_out), .Q(D2_0[7:6]));
  Register_2Bit register_2bit_31 (.IN(and_69_out), .Clock(or_31_out), .Q(D2_0[9:8]));
  Register_2Bit register_2bit_32 (.IN(and_69_out), .Clock(or_32_out), .Q(D2_0[11:10]));
  Register_2Bit register_2bit_33 (.IN(and_69_out), .Clock(or_33_out), .Q(register_2bit_33_q));
  Register_2Bit register_2bit_34 (.IN(and_69_out), .Clock(or_34_out), .Q(register_2bit_34_q));
  Register_2Bit register_2bit_35 (.IN(and_69_out), .Clock(or_35_out), .Q(D1_3[1:0]));
  Register_2Bit register_2bit_36 (.IN(and_69_out), .Clock(or_36_out), .Q(D1_3[3:2]));
  Register_2Bit register_2bit_37 (.IN(and_69_out), .Clock(or_37_out), .Q(D1_3[5:4]));
  Register_2Bit register_2bit_38 (.IN(and_69_out), .Clock(or_38_out), .Q(D1_3[7:6]));
  Register_2Bit register_2bit_39 (.IN(and_69_out), .Clock(or_39_out), .Q(D1_3[9:8]));
  Register_2Bit register_2bit_40 (.IN(and_69_out), .Clock(or_40_out), .Q(D1_3[11:10]));
  Register_2Bit register_2bit_41 (.IN(and_69_out), .Clock(or_41_out), .Q(register_2bit_41_q));
  Register_2Bit register_2bit_42 (.IN(and_69_out), .Clock(or_42_out), .Q(register_2bit_42_q));
  Register_2Bit register_2bit_43 (.IN(and_69_out), .Clock(or_43_out), .Q(D1_2[1:0]));
  Register_2Bit register_2bit_44 (.IN(and_69_out), .Clock(or_44_out), .Q(D1_2[3:2]));
  Register_2Bit register_2bit_45 (.IN(and_69_out), .Clock(or_45_out), .Q(D1_2[5:4]));
  Register_2Bit register_2bit_46 (.IN(and_69_out), .Clock(or_46_out), .Q(D1_2[7:6]));
  Register_2Bit register_2bit_47 (.IN(and_69_out), .Clock(or_47_out), .Q(D1_2[9:8]));
  Register_2Bit register_2bit_48 (.IN(and_69_out), .Clock(or_48_out), .Q(D1_2[11:10]));
  Register_2Bit register_2bit_49 (.IN(and_69_out), .Clock(or_49_out), .Q(register_2bit_49_q));
  Register_2Bit register_2bit_50 (.IN(and_69_out), .Clock(or_50_out), .Q(register_2bit_50_q));
  Register_2Bit register_2bit_51 (.IN(and_69_out), .Clock(or_51_out), .Q(D1_1[1:0]));
  Register_2Bit register_2bit_52 (.IN(and_69_out), .Clock(or_52_out), .Q(D1_1[3:2]));
  Register_2Bit register_2bit_53 (.IN(and_69_out), .Clock(or_53_out), .Q(D1_1[5:4]));
  Register_2Bit register_2bit_54 (.IN(and_69_out), .Clock(or_54_out), .Q(D1_1[7:6]));
  Register_2Bit register_2bit_55 (.IN(and_69_out), .Clock(or_55_out), .Q(D1_1[9:8]));
  Register_2Bit register_2bit_56 (.IN(and_69_out), .Clock(or_56_out), .Q(D1_1[11:10]));
  Register_2Bit register_2bit_57 (.IN(and_69_out), .Clock(or_57_out), .Q(register_2bit_57_q));
  Register_2Bit register_2bit_58 (.IN(and_69_out), .Clock(or_58_out), .Q(register_2bit_58_q));
  Register_2Bit register_2bit_59 (.IN(and_69_out), .Clock(or_59_out), .Q(D1_0[1:0]));
  Register_2Bit register_2bit_60 (.IN(and_69_out), .Clock(or_60_out), .Q(D1_0[3:2]));
  Register_2Bit register_2bit_61 (.IN(and_69_out), .Clock(or_61_out), .Q(D1_0[5:4]));
  Register_2Bit register_2bit_62 (.IN(and_69_out), .Clock(or_62_out), .Q(D1_0[7:6]));
  Register_2Bit register_2bit_63 (.IN(and_69_out), .Clock(or_63_out), .Q(D1_0[9:8]));
  Register_2Bit register_2bit_64 (.IN(and_69_out), .Clock(or_64_out), .Q(D1_0[11:10]));
  Register_3Bit register_3bit_1 (.IN(and_1_out), .Clock(or_65_out), .OUT(State_out));
  Register_3Bit register_3bit_2 (.IN(and_2_out), .Clock(or_66_out), .OUT(B_C__1_out));
  Register_3Bit register_3bit_3 (.IN(and_2_out), .Clock(or_67_out), .OUT(B_C__2_out));
  Multiplexer_64 multiplexer_64_1 (
    .out_66(Read_out), .in_1(D1_0[11:10]), .in_2(D1_0[9:8]), .in_3(D1_0[7:6]), .in_4(D1_0[5:4]),
    .in_5(D1_0[3:2]), .in_6(D1_0[1:0]), .in_7(register_2bit_58_q), .in_8(register_2bit_57_q),
    .in_9(D1_1[11:10]), .in_10(D1_1[9:8]), .in_11(D1_1[7:6]), .in_12(D1_1[5:4]), .in_13(D1_1[3:2]),
    .in_14(D1_1[1:0]), .in_15(register_2bit_50_q), .in_16(register_2bit_49_q), .in_17(D1_2[11:10]),
    .in_18(D1_2[9:8]), .in_19(D1_2[7:6]), .in_20(D1_2[5:4]), .in_21(D1_2[3:2]), .in_22(D1_2[1:0]),
    .in_23(register_2bit_42_q), .in_24(register_2bit_41_q), .in_25(D1_3[11:10]), .in_26(D1_3[9:8]),
    .in_27(D1_3[7:6]), .in_28(D1_3[5:4]), .in_29(D1_3[3:2]), .in_30(D1_3[1:0]), .in_31(register_2bit_34_q),
    .in_32(register_2bit_33_q), .in_33(D2_0[11:10]), .in_34(D2_0[9:8]), .in_35(D2_0[7:6]), .in_36(D2_0[5:4]),
    .in_37(D2_0[3:2]), .in_38(D2_0[1:0]), .in_39(register_2bit_26_q), .in_40(register_2bit_25_q),
    .in_41(D2_1[11:10]), .in_42(D2_1[9:8]), .in_43(D2_1[7:6]), .in_44(D2_1[5:4]), .in_45(D2_1[3:2]),
    .in_46(D2_1[1:0]), .in_47(register_2bit_18_q), .in_48(register_2bit_17_q), .in_49(D2_2[11:10]),
    .in_50(D2_2[9:8]), .in_51(D2_2[7:6]), .in_52(D2_2[5:4]), .in_53(D2_2[3:2]), .in_54(D2_2[1:0]),
    .in_55(register_2bit_10_q), .in_56(register_2bit_9_q), .in_57(D2_3[11:10]), .in_58(D2_3[9:8]),
    .in_59(D2_3[7:6]), .in_60(D2_3[5:4]), .in_61(D2_3[3:2]), .in_62(D2_3[1:0]), .in_63(register_2bit_2_q),
    .in_64(register_2bit_1_q), .Select(Register));

  // Notes on the sheet:
  //   Grid Memory
  //   State
  //   Boat count player 1
  //   Boat count player 2
  //   |------------------------------------------- Display out 2 ----------------------------------------------|
  //   |------------------------------------------- Display out 1 ----------------------------------------------|
endmodule

module AttackKeeper (
  input  [4:0] A1,
  input  [4:0] A2,
  input  [2:0] State,
  output [5:0] Out
);

  wire [4:0] and_1_out, and_2_out;

  assign and_1_out = A1 & ~{5{State[1]}};  // AND_Gate and_1, 5 bits wide
  assign and_2_out = A2 & {5{State[1]}};  // AND_Gate and_2, 5 bits wide
  assign Out[4:0] = and_1_out | and_2_out;  // OR_Gate or_1, 5 bits wide
  xor xor_1 (Out[5], State[1], State[2]);
endmodule

module StateManager (
  input  A1,
  input  A2,
  input  [2:0] State,
  input  [2:0] S_C_1,
  input  [2:0] S_C_2,
  output [2:0] New_State,
  output Reset_key_pads,
  output New_Game
);

  wire and_1_out, and_2_out, and_3_out, and_4_out, and_5_out, and_6_out, and_8_out, and_9_out, and_10_out,
       nor_1_out, nor_2_out, or_1_out, or_2_out, or_3_out, xor_1_out, xor_2_out;

  and and_1 (and_1_out, ~S_C_1[0], S_C_1[1], S_C_1[2]);  // AND_Gate
  nor nor_1 (nor_1_out, S_C_1[0], S_C_1[1], S_C_1[2]);
  and and_2 (and_2_out, ~S_C_2[0], S_C_2[1], S_C_2[2]);  // AND_Gate
  nor nor_2 (nor_2_out, S_C_2[0], S_C_2[1], S_C_2[2]);
  and and_3 (and_3_out, A1, ~State[1]);  // AND_Gate
  and and_4 (and_4_out, State[1], A2);
  and and_5 (and_5_out, and_1_out, ~State[1]);  // AND_Gate
  and and_6 (and_6_out, State[1], and_2_out);
  or or_1 (or_1_out, nor_1_out, nor_2_out);
  or or_2 (or_2_out, and_3_out, and_4_out);
  or or_3 (or_3_out, and_5_out, and_6_out);
  and and_7 (New_State[0], or_2_out, ~State[0]);  // AND_Gate
  xor xor_1 (xor_1_out, or_3_out, State[1]);
  xor xor_2 (xor_2_out, State[1], State[0]);
  and and_8 (and_8_out, xor_1_out, ~State[2]);  // AND_Gate
  and and_9 (and_9_out, State[2], xor_2_out);
  and and_10 (and_10_out, and_1_out, and_2_out);
  and and_11 (New_Game, or_1_out, State[2]);
  or or_4 (New_State[1], and_8_out, and_9_out);
  or or_5 (New_State[2], State[2], and_10_out);

  assign Reset_key_pads = State[0];
endmodule

module S_C_DisplayDriver (
  input  [2:0] State,
  output [3:0] Out
);

  not not_1 (Out[3], 1'b1);

  assign Out[2:0] = State;
endmodule
