// Logisim project circuit.circ as structural Verilog: 4 circuits, main circuit main
module main (
  input  [5:0] in_1,
  input  [2:0] in_2
);

  wire clock_1_out, display_driver_1_a, display_driver_1_b, display_driver_1_c, display_driver_1_d,
       display_driver_1_i1, display_driver_1_out_5, display_driver_1_out_6, display_driver_1_out_7,
       display_driver_1_out_8, display_driver_1_out_9, display_driver_1_out_10, display_driver_1_out_11,
       display_driver_1_out_12, display_driver_1_out_13, display_driver_1_out_14, display_driver_1_out_15,
       display_driver_1_out_16, display_driver_1_out_17, display_driver_1_out_18, display_driver_1_out_19,
       display_driver_1_out_20, display_driver_1_out_21, display_driver_1_out_22, display_driver_1_out_23,
       display_driver_1_out_24, display_driver_1_out_25, display_driver_1_out_26, display_driver_1_out_27,
       display_driver_1_out_28, display_driver_1_out_29, display_driver_1_out_31, display_driver_1_out_32,
       display_driver_1_out_33, display_driver_1_out_34, display_driver_1_out_35, display_driver_1_out_37,
       display_driver_1_out_38, display_driver_1_out_39, display_driver_1_out_40, display_driver_1_out_41,
       display_driver_1_out_43, display_driver_1_out_44, display_driver_1_out_45, display_driver_1_out_46,
       display_driver_1_out_49, display_driver_1_out_50, display_driver_1_out_51, display_driver_1_out_52,
       display_driver_1_out_53, display_driver_1_out_54, display_driver_1_out_55, display_driver_1_out_56,
       display_driver_1_out_57, display_driver_1_out_58, display_driver_1_out_59, display_driver_1_out_60,
       display_driver_1_out_61, display_driver_1_out_62, display_driver_1_out_63, display_driver_1_out_64,
       display_driver_1_out_65, display_driver_1_out_66, display_driver_1_out_67, display_driver_1_out_68,
       display_driver_1_out_69, display_driver_1_out_70, display_driver_1_out_71, display_driver_1_out_72,
       display_driver_1_out_73, display_driver_1_out_74, display_driver_1_out_75, display_driver_1_out_76,
       display_driver_1_out_77, display_driver_1_out_78, display_driver_1_out_79, display_driver_1_out_80,
       display_driver_1_out_81, display_driver_1_out_82, display_driver_1_out_83, display_driver_1_out_84,
       display_driver_1_out_85, display_driver_1_out_86, display_driver_1_out_87, display_driver_1_out_88,
       display_driver_1_out_89, display_driver_1_out_90, display_driver_1_out_91, display_driver_1_out_92,
       display_driver_1_out_93, display_driver_1_out_94, display_driver_1_out_95, display_driver_1_out_96,
       display_driver_1_out_97, display_driver_1_out_98, display_driver_1_out_99, display_driver_1_out_100,
       display_driver_2_a, display_driver_2_b, display_driver_2_c, display_driver_2_d, display_driver_2_i1,
       display_driver_2_out_5, display_driver_2_out_6, display_driver_2_out_7, display_driver_2_out_8,
       display_driver_2_out_9, display_driver_2_out_10, display_driver_2_out_11, display_driver_2_out_12,
       display_driver_2_out_13, display_driver_2_out_14, display_driver_2_out_15, display_driver_2_out_16,
       display_driver_2_out_17, display_driver_2_out_18, display_driver_2_out_19, display_driver_2_out_20,
       display_driver_2_out_21, display_driver_2_out_22, display_driver_2_out_23, display_driver_2_out_24,
       display_driver_2_out_25, display_driver_2_out_26, display_driver_2_out_27, display_driver_2_out_28,
       display_driver_2_out_29, display_driver_2_out_31, display_driver_2_out_32, display_driver_2_out_33,
       display_driver_2_out_34, display_driver_2_out_35, display_driver_2_out_37, display_driver_2_out_38,
       display_driver_2_out_39, display_driver_2_out_40, display_driver_2_out_41, display_driver_2_out_43,
       display_driver_2_out_44, display_driver_2_out_45, display_driver_2_out_46, display_driver_2_out_49,
       display_driver_2_out_50, display_driver_2_out_51, display_driver_2_out_52, display_driver_2_out_53,
       display_driver_2_out_54, display_driver_2_out_55, display_driver_2_out_56, display_driver_2_out_57,
       display_driver_2_out_58, display_driver_2_out_59, display_driver_2_out_60, display_driver_2_out_61,
       display_driver_2_out_62, display_driver_2_out_63, display_driver_2_out_64, display_driver_2_out_65,
       display_driver_2_out_66, display_driver_2_out_67, display_driver_2_out_68, display_driver_2_out_69,
       display_driver_2_out_70, display_driver_2_out_71, display_driver_2_out_72, display_driver_2_out_73,
       display_driver_2_out_74, display_driver_2_out_75, display_driver_2_out_76, display_driver_2_out_77,
       display_driver_2_out_78, display_driver_2_out_79, display_driver_2_out_80, display_driver_2_out_81,
       display_driver_2_out_82, display_driver_2_out_83, display_driver_2_out_84, display_driver_2_out_85,
       display_driver_2_out_86, display_driver_2_out_87, display_driver_2_out_88, display_driver_2_out_89,
       display_driver_2_out_90, display_driver_2_out_91, display_driver_2_out_92, display_driver_2_out_93,
       display_driver_2_out_94, display_driver_2_out_95, display_driver_2_out_96, display_driver_2_out_97,
       display_driver_2_out_98, display_driver_2_out_99, display_driver_2_out_100, shipcountmanager_2_p3,
       shipcountmanager_2_p4;
  wire [1:0] attackprocessor_1_valueout, ReadOut;
  wire [2:0] StateOut;
  wire [11:0] memory_1_p9, memory_1_p10, memory_1_p11, memory_1_p12, memory_1_p13, memory_1_p14,
       memory_1_p15, memory_1_p16;

  // ShipCountManager shipcountmanager_1: pin names not known; wires that end beside it: ReadOut
  AttackProcessor attackprocessor_1 (.ValueIn(ReadOut), .State(StateOut), .ValueOut(attackprocessor_1_valueout));
  // ShipCountManager shipcountmanager_2: pin names not known; wires that end beside it: attackprocessor_1_valueout, StateOut, shipcountmanager_2_p3, shipcountmanager_2_p4
  Clock clock_1 (.out(clock_1_out));
  // Memory memory_1: pin names not known; wires that end beside it: in_1, in_1, attackprocessor_1_valueout, in_2, shipcountmanager_2_p3, shipcountmanager_2_p4, clock_1_out, ReadOut, memory_1_p9, memory_1_p10, memory_1_p11, memory_1_p12, memory_1_p13, memory_1_p14, memory_1_p15, memory_1_p16, StateOut
  LED led_1 (.in(display_driver_1_out_11));
  LED led_2 (.in(display_driver_1_out_12));
  LED led_3 (.in(display_driver_1_out_5));
  LED led_4 (.in(display_driver_1_out_23));
  LED led_5 (.in(display_driver_1_out_18));
  LED led_6 (.in(display_driver_1_out_17));
  LED led_7 (.in(display_driver_1_a));
  LED led_8 (.in(display_driver_1_out_29));
  LED led_9 (.in(display_driver_1_out_35));
  LED led_10 (.in(display_driver_1_out_41));
  LED led_11 (.in(display_driver_1_c));
  LED led_12 (.in(display_driver_1_i1));
  LED led_13 (.in(display_driver_1_out_60));
  LED led_14 (.in(display_driver_1_out_53));
  LED led_15 (.in(display_driver_1_out_59));
  LED led_16 (.in(display_driver_1_out_65));
  LED led_17 (.in(display_driver_1_out_66));
  LED led_18 (.in(display_driver_1_out_71));
  LED led_19 (.in(display_driver_1_out_77));
  LED led_20 (.in(display_driver_1_out_83));
  LED led_21 (.in(display_driver_1_out_84));
  LED led_22 (.in(display_driver_1_out_95));
  LED led_23 (.in(display_driver_1_out_89));
  LED led_24 (.in(display_driver_1_out_90));
  LED led_25 (.in(display_driver_2_out_5));
  LED led_26 (.in(display_driver_2_out_11));
  LED led_27 (.in(display_driver_2_out_12));
  LED led_28 (.in(display_driver_2_out_18));
  LED led_29 (.in(display_driver_2_out_23));
  LED led_30 (.in(display_driver_2_out_17));
  LED led_31 (.in(display_driver_2_a));
  LED led_32 (.in(display_driver_2_out_29));
  LED led_33 (.in(display_driver_2_out_35));
  LED led_34 (.in(display_driver_2_c));
  LED led_35 (.in(display_driver_2_out_41));
  LED led_36 (.in(display_driver_2_i1));
  LED led_37 (.in(display_driver_2_out_60));
  LED led_38 (.in(display_driver_2_out_53));
  LED led_39 (.in(display_driver_2_out_59));
  LED led_40 (.in(display_driver_2_out_66));
  LED led_41 (.in(display_driver_2_out_65));
  LED led_42 (.in(display_driver_2_out_71));
  LED led_43 (.in(display_driver_2_out_77));
  LED led_44 (.in(display_driver_2_out_83));
  LED led_45 (.in(display_driver_2_out_84));
  LED led_46 (.in(display_driver_2_out_90));
  LED led_47 (.in(display_driver_2_out_95));
  LED led_48 (.in(display_driver_2_out_89));
  LED led_49 (.in(display_driver_1_out_7));
  LED led_50 (.in(display_driver_1_out_6));
  LED led_51 (.in(display_driver_1_out_13));
  LED led_52 (.in(display_driver_1_out_19));
  LED led_53 (.in(display_driver_1_out_24));
  LED led_54 (.in(display_driver_1_out_25));
  LED led_55 (.in(display_driver_1_b));
  LED led_56 (.in(display_driver_1_out_37));
  LED led_57 (.in(display_driver_1_out_31));
  LED led_58 (.in(display_driver_1_d));
  LED led_59 (.in(display_driver_1_out_49));
  LED led_60 (.in(display_driver_1_out_43));
  LED led_61 (.in(display_driver_1_out_54));
  LED led_62 (.in(display_driver_1_out_61));
  LED led_63 (.in(display_driver_1_out_55));
  LED led_64 (.in(display_driver_1_out_73));
  LED led_65 (.in(display_driver_1_out_72));
  LED led_66 (.in(display_driver_1_out_67));
  LED led_67 (.in(display_driver_1_out_85));
  LED led_68 (.in(display_driver_1_out_79));
  LED led_69 (.in(display_driver_1_out_78));
  LED led_70 (.in(display_driver_1_out_96));
  LED led_71 (.in(display_driver_1_out_97));
  LED led_72 (.in(display_driver_1_out_91));
  LED led_73 (.in(display_driver_2_out_13));
  LED led_74 (.in(display_driver_2_out_6));
  LED led_75 (.in(display_driver_2_out_7));
  LED led_76 (.in(display_driver_2_out_24));
  LED led_77 (.in(display_driver_2_out_25));
  LED led_78 (.in(display_driver_2_out_19));
  LED led_79 (.in(display_driver_2_out_31));
  LED led_80 (.in(display_driver_2_b));
  LED led_81 (.in(display_driver_2_out_37));
  LED led_82 (.in(display_driver_2_d));
  LED led_83 (.in(display_driver_2_out_49));
  LED led_84 (.in(display_driver_2_out_43));
  LED led_85 (.in(display_driver_2_out_54));
  LED led_86 (.in(display_driver_2_out_55));
  LED led_87 (.in(display_driver_2_out_61));
  LED led_88 (.in(display_driver_2_out_67));
  LED led_89 (.in(display_driver_2_out_73));
  LED led_90 (.in(display_driver_2_out_72));
  LED led_91 (.in(display_driver_2_out_85));
  LED led_92 (.in(display_driver_2_out_78));
  LED led_93 (.in(display_driver_2_out_79));
  LED led_94 (.in(display_driver_2_out_96));
  LED led_95 (.in(display_driver_2_out_97));
  LED led_96 (.in(display_driver_2_out_91));
  LED led_97 (.in(display_driver_1_out_14));
  LED led_98 (.in(display_driver_1_out_15));
  LED led_99 (.in(display_driver_1_out_9));
  LED led_100 (.in(display_driver_1_out_8));
  LED led_101 (.in(display_driver_1_out_26));
  LED led_102 (.in(display_driver_1_out_20));
  LED led_103 (.in(display_driver_1_out_27));
  LED led_104 (.in(display_driver_1_out_21));
  LED led_105 (.in(display_driver_1_out_32));
  LED led_106 (.in(display_driver_1_out_38));
  LED led_107 (.in(display_driver_1_out_39));
  LED led_108 (.in(display_driver_1_out_33));
  LED led_109 (.in(display_driver_1_out_50));
  LED led_110 (.in(display_driver_1_out_44));
  LED led_111 (.in(display_driver_1_out_45));
  LED led_112 (.in(display_driver_1_out_51));
  LED led_113 (.in(display_driver_1_out_57));
  LED led_114 (.in(display_driver_1_out_56));
  LED led_115 (.in(display_driver_1_out_62));
  LED led_116 (.in(display_driver_1_out_63));
  LED led_117 (.in(display_driver_1_out_75));
  LED led_118 (.in(display_driver_1_out_68));
  LED led_119 (.in(display_driver_1_out_74));
  LED led_120 (.in(display_driver_1_out_69));
  LED led_121 (.in(display_driver_1_out_86));
  LED led_122 (.in(display_driver_1_out_80));
  LED led_123 (.in(display_driver_1_out_87));
  LED led_124 (.in(display_driver_1_out_81));
  LED led_125 (.in(display_driver_1_out_93));
  LED led_126 (.in(display_driver_1_out_98));
  LED led_127 (.in(display_driver_1_out_92));
  LED led_128 (.in(display_driver_1_out_99));
  LED led_129 (.in(display_driver_2_out_9));
  LED led_130 (.in(display_driver_2_out_8));
  LED led_131 (.in(display_driver_2_out_15));
  LED led_132 (.in(display_driver_2_out_14));
  LED led_133 (.in(display_driver_2_out_27));
  LED led_134 (.in(display_driver_2_out_21));
  LED led_135 (.in(display_driver_2_out_20));
  LED led_136 (.in(display_driver_2_out_26));
  LED led_137 (.in(display_driver_2_out_39));
  LED led_138 (.in(display_driver_2_out_33));
  LED led_139 (.in(display_driver_2_out_32));
  LED led_140 (.in(display_driver_2_out_38));
  LED led_141 (.in(display_driver_2_out_45));
  LED led_142 (.in(display_driver_2_out_44));
  LED led_143 (.in(display_driver_2_out_50));
  LED led_144 (.in(display_driver_2_out_51));
  LED led_145 (.in(display_driver_2_out_57));
  LED led_146 (.in(display_driver_2_out_56));
  LED led_147 (.in(display_driver_2_out_62));
  LED led_148 (.in(display_driver_2_out_63));
  LED led_149 (.in(display_driver_2_out_74));
  LED led_150 (.in(display_driver_2_out_69));
  LED led_151 (.in(display_driver_2_out_75));
  LED led_152 (.in(display_driver_2_out_68));
  LED led_153 (.in(display_driver_2_out_87));
  LED led_154 (.in(display_driver_2_out_80));
  LED led_155 (.in(display_driver_2_out_86));
  LED led_156 (.in(display_driver_2_out_81));
  LED led_157 (.in(display_driver_2_out_92));
  LED led_158 (.in(display_driver_2_out_98));
  LED led_159 (.in(display_driver_2_out_93));
  LED led_160 (.in(display_driver_2_out_99));
  LED led_161 (.in(display_driver_1_out_16));
  LED led_162 (.in(display_driver_1_out_10));
  Display_Driver display_driver_1 (
    .out_11(display_driver_1_out_11), .out_5(display_driver_1_out_5), .out_17(display_driver_1_out_17),
    .out_23(display_driver_1_out_23), .out_6(display_driver_1_out_6), .out_12(display_driver_1_out_12),
    .out_18(display_driver_1_out_18), .out_24(display_driver_1_out_24), .out_7(display_driver_1_out_7),
    .out_13(display_driver_1_out_13), .out_19(display_driver_1_out_19), .out_25(display_driver_1_out_25),
    .out_8(display_driver_1_out_8), .out_9(display_driver_1_out_9), .out_10(display_driver_1_out_10),
    .out_14(display_driver_1_out_14), .out_15(display_driver_1_out_15), .out_16(display_driver_1_out_16),
    .out_20(display_driver_1_out_20), .out_21(display_driver_1_out_21), .out_22(display_driver_1_out_22),
    .out_26(display_driver_1_out_26), .out_27(display_driver_1_out_27), .out_28(display_driver_1_out_28),
    .out_29(display_driver_1_out_29), .B(display_driver_1_b), .out_31(display_driver_1_out_31),
    .out_32(display_driver_1_out_32), .out_33(display_driver_1_out_33), .out_34(display_driver_1_out_34),
    .out_35(display_driver_1_out_35), .A(display_driver_1_a), .out_37(display_driver_1_out_37),
    .out_38(display_driver_1_out_38), .out_39(display_driver_1_out_39), .out_40(display_driver_1_out_40),
    .out_41(display_driver_1_out_41), .C(display_driver_1_c), .out_43(display_driver_1_out_43),
    .out_44(display_driver_1_out_44), .out_45(display_driver_1_out_45), .out_46(display_driver_1_out_46),
    .i1(display_driver_1_i1), .D(display_driver_1_d), .out_49(display_driver_1_out_49),
    .out_50(display_driver_1_out_50), .out_51(display_driver_1_out_51), .out_52(display_driver_1_out_52),
    .out_53(display_driver_1_out_53), .out_54(display_driver_1_out_54), .out_55(display_driver_1_out_55),
    .out_56(display_driver_1_out_56), .out_57(display_driver_1_out_57), .out_58(display_driver_1_out_58),
    .out_59(display_driver_1_out_59), .out_60(display_driver_1_out_60), .out_61(display_driver_1_out_61),
    .out_62(display_driver_1_out_62), .out_63(display_driver_1_out_63), .out_64(display_driver_1_out_64),
    .out_65(display_driver_1_out_65), .out_66(display_driver_1_out_66), .out_67(display_driver_1_out_67),
    .out_68(display_driver_1_out_68), .out_69(display_driver_1_out_69), .out_70(display_driver_1_out_70),
    .out_71(display_driver_1_out_71), .out_72(display_driver_1_out_72), .out_73(display_driver_1_out_73),
    .out_74(display_driver_1_out_74), .out_75(display_driver_1_out_75), .out_76(display_driver_1_out_76),
    .out_77(display_driver_1_out_77), .out_78(display_driver_1_out_78), .out_79(display_driver_1_out_79),
    .out_80(display_driver_1_out_80), .out_81(display_driver_1_out_81), .out_82(display_driver_1_out_82),
    .out_83(display_driver_1_out_83), .out_84(display_driver_1_out_84), .out_85(display_driver_1_out_85),
    .out_86(display_driver_1_out_86), .out_87(display_driver_1_out_87), .out_88(display_driver_1_out_88),
    .out_89(display_driver_1_out_89), .out_90(display_driver_1_out_90), .out_91(display_driver_1_out_91),
    .out_92(display_driver_1_out_92), .out_93(display_driver_1_out_93), .out_94(display_driver_1_out_94),
    .out_95(display_driver_1_out_95), .out_96(display_driver_1_out_96), .out_97(display_driver_1_out_97),
    .out_98(display_driver_1_out_98), .out_99(display_driver_1_out_99), .out_100(display_driver_1_out_100),
    .in_1(memory_1_p9), .in_2(memory_1_p10), .in_3(memory_1_p11), .in_4(memory_1_p12));
  LED led_163 (.in(display_driver_1_out_28));
  LED led_164 (.in(display_driver_1_out_22));
  LED led_165 (.in(display_driver_1_out_40));
  LED led_166 (.in(display_driver_1_out_34));
  LED led_167 (.in(display_driver_1_out_52));
  LED led_168 (.in(display_driver_1_out_46));
  LED led_169 (.in(display_driver_1_out_64));
  LED led_170 (.in(display_driver_1_out_58));
  LED led_171 (.in(display_driver_1_out_70));
  LED led_172 (.in(display_driver_1_out_76));
  LED led_173 (.in(display_driver_1_out_88));
  LED led_174 (.in(display_driver_1_out_82));
  LED led_175 (.in(display_driver_1_out_94));
  LED led_176 (.in(display_driver_1_out_100));
  LED led_177 (.in(display_driver_2_out_10));
  LED led_178 (.in(display_driver_2_out_16));
  Display_Driver display_driver_2 (
    .out_11(display_driver_2_out_11), .out_5(display_driver_2_out_5), .out_17(display_driver_2_out_17),
    .out_23(display_driver_2_out_23), .out_6(display_driver_2_out_6), .out_12(display_driver_2_out_12),
    .out_18(display_driver_2_out_18), .out_24(display_driver_2_out_24), .out_7(display_driver_2_out_7),
    .out_13(display_driver_2_out_13), .out_19(display_driver_2_out_19), .out_25(display_driver_2_out_25),
    .out_8(display_driver_2_out_8), .out_9(display_driver_2_out_9), .out_10(display_driver_2_out_10),
    .out_14(display_driver_2_out_14), .out_15(display_driver_2_out_15), .out_16(display_driver_2_out_16),
    .out_20(display_driver_2_out_20), .out_21(display_driver_2_out_21), .out_22(display_driver_2_out_22),
    .out_26(display_driver_2_out_26), .out_27(display_driver_2_out_27), .out_28(display_driver_2_out_28),
    .out_29(display_driver_2_out_29), .B(display_driver_2_b), .out_31(display_driver_2_out_31),
    .out_32(display_driver_2_out_32), .out_33(display_driver_2_out_33), .out_34(display_driver_2_out_34),
    .out_35(display_driver_2_out_35), .A(display_driver_2_a), .out_37(display_driver_2_out_37),
    .out_38(display_driver_2_out_38), .out_39(display_driver_2_out_39), .out_40(display_driver_2_out_40),
    .out_41(display_driver_2_out_41), .C(display_driver_2_c), .out_43(display_driver_2_out_43),
    .out_44(display_driver_2_out_44), .out_45(display_driver_2_out_45), .out_46(display_driver_2_out_46),
    .i1(display_driver_2_i1), .D(display_driver_2_d), .out_49(display_driver_2_out_49),
    .out_50(display_driver_2_out_50), .out_51(display_driver_2_out_51), .out_52(display_driver_2_out_52),
    .out_53(display_driver_2_out_53), .out_54(display_driver_2_out_54), .out_55(display_driver_2_out_55),
    .out_56(display_driver_2_out_56), .out_57(display_driver_2_out_57), .out_58(display_driver_2_out_58),
    .out_59(display_driver_2_out_59), .out_60(display_driver_2_out_60), .out_61(display_driver_2_out_61),
    .out_62(display_driver_2_out_62), .out_63(display_driver_2_out_63), .out_64(display_driver_2_out_64),
    .out_65(display_driver_2_out_65), .out_66(display_driver_2_out_66), .out_67(display_driver_2_out_67),
    .out_68(display_driver_2_out_68), .out_69(display_driver_2_out_69), .out_70(display_driver_2_out_70),
    .out_71(display_driver_2_out_71), .out_72(display_driver_2_out_72), .out_73(display_driver_2_out_73),
    .out_74(display_driver_2_out_74), .out_75(display_driver_2_out_75), .out_76(display_driver_2_out_76),
    .out_77(display_driver_2_out_77), .out_78(display_driver_2_out_78), .out_79(display_driver_2_out_79),
    .out_80(display_driver_2_out_80), .out_81(display_driver_2_out_81), .out_82(display_driver_2_out_82),
    .out_83(display_driver_2_out_83), .out_84(display_driver_2_out_84), .out_85(display_driver_2_out_85),
    .out_86(display_driver_2_out_86), .out_87(display_driver_2_out_87), .out_88(display_driver_2_out_88),
    .out_89(display_driver_2_out_89), .out_90(display_driver_2_out_90), .out_91(display_driver_2_out_91),
    .out_92(display_driver_2_out_92), .out_93(display_driver_2_out_93), .out_94(display_driver_2_out_94),
    .out_95(display_driver_2_out_95), .out_96(display_driver_2_out_96), .out_97(display_driver_2_out_97),
    .out_98(display_driver_2_out_98), .out_99(display_driver_2_out_99), .out_100(display_driver_2_out_100),
    .in_1(memory_1_p13), .in_2(memory_1_p14), .in_3(memory_1_p15), .in_4(memory_1_p16));
  LED led_179 (.in(display_driver_2_out_28));
  LED led_180 (.in(display_driver_2_out_22));
  LED led_181 (.in(display_driver_2_out_40));
  LED led_182 (.in(display_driver_2_out_34));
  LED led_183 (.in(display_driver_2_out_46));
  LED led_184 (.in(display_driver_2_out_52));
  LED led_185 (.in(display_driver_2_out_58));
  LED led_186 (.in(display_driver_2_out_64));
  LED led_187 (.in(display_driver_2_out_70));
  LED led_188 (.in(display_driver_2_out_76));
  LED led_189 (.in(display_driver_2_out_88));
  LED led_190 (.in(display_driver_2_out_82));
  LED led_191 (.in(display_driver_2_out_100));
  LED led_192 (.in(display_driver_2_out_94));
endmodule

module Display_Driver (
  input  [11:0] in_1,
  input  [11:0] in_2,
  input  [11:0] in_3,
  input  [11:0] in_4,
  output out_5,
  output out_6,
  output out_7,
  output out_8,
  output out_9,
  output out_10,
  output out_11,
  output out_12,
  output out_13,
  output out_14,
  output out_15,
  output out_16,
  output out_17,
  output out_18,
  output out_19,
  output out_20,
  output out_21,
  output out_22,
  output out_23,
  output out_24,
  output out_25,
  output out_26,
  output out_27,
  output out_28,
  output out_29,
  output B,
  output out_31,
  output out_32,
  output out_33,
  output out_34,
  output out_35,
  output A,
  output out_37,
  output out_38,
  output out_39,
  output out_40,
  output out_41,
  output C,
  output out_43,
  output out_44,
  output out_45,
  output out_46,
  output i1,
  output D,
  output out_49,
  output out_50,
  output out_51,
  output out_52,
  output out_53,
  output out_54,
  output out_55,
  output out_56,
  output out_57,
  output out_58,
  output out_59,
  output out_60,
  output out_61,
  output out_62,
  output out_63,
  output out_64,
  output out_65,
  output out_66,
  output out_67,
  output out_68,
  output out_69,
  output out_70,
  output out_71,
  output out_72,
  output out_73,
  output out_74,
  output out_75,
  output out_76,
  output out_77,
  output out_78,
  output out_79,
  output out_80,
  output out_81,
  output out_82,
  output out_83,
  output out_84,
  output out_85,
  output out_86,
  output out_87,
  output out_88,
  output out_89,
  output out_90,
  output out_91,
  output out_92,
  output out_93,
  output out_94,
  output out_95,
  output out_96,
  output out_97,
  output out_98,
  output out_99,
  output out_100
);

  xor xor_1 (out_11, in_1[11], in_1[10]);
  xor xor_2 (i1, in_2[11], in_2[10]);
  xor xor_3 (out_59, in_3[11], in_3[10]);
  xor xor_4 (out_83, in_4[11], in_4[10]);
  xor xor_5 (out_12, in_1[9], in_1[8]);
  xor xor_6 (A, in_2[9], in_2[8]);
  xor xor_7 (out_60, in_3[9], in_3[8]);
  xor xor_8 (out_84, in_4[9], in_4[8]);
  xor xor_9 (out_13, in_1[7], in_1[6]);
  xor xor_10 (out_37, in_2[7], in_2[6]);
  xor xor_11 (out_61, in_3[7], in_3[6]);
  xor xor_12 (out_85, in_4[7], in_4[6]);
  xor xor_13 (out_14, in_1[5], in_1[4]);
  xor xor_14 (out_38, in_2[5], in_2[4]);
  xor xor_15 (out_62, in_3[5], in_3[4]);
  xor xor_16 (out_86, in_4[5], in_4[4]);
  xor xor_17 (out_15, in_1[3], in_1[2]);
  xor xor_18 (out_39, in_2[3], in_2[2]);
  xor xor_19 (out_63, in_3[3], in_3[2]);
  xor xor_20 (out_87, in_4[3], in_4[2]);
  xor xor_21 (out_16, in_1[1], in_1[0]);
  xor xor_22 (out_40, in_2[1], in_2[0]);
  xor xor_23 (out_64, in_3[1], in_3[0]);
  xor xor_24 (out_88, in_4[1], in_4[0]);

  assign B = in_2[8];
  assign C = in_2[8];
  assign D = A;
  assign out_5 = in_1[10];
  assign out_6 = in_1[8];
  assign out_7 = in_1[6];
  assign out_8 = in_1[4];
  assign out_9 = in_1[2];
  assign out_10 = in_1[0];
  assign out_17 = in_1[10];
  assign out_18 = in_1[8];
  assign out_19 = in_1[6];
  assign out_20 = in_1[4];
  assign out_21 = in_1[2];
  assign out_22 = in_1[0];
  assign out_23 = out_11;
  assign out_24 = out_12;
  assign out_25 = out_13;
  assign out_26 = out_14;
  assign out_27 = out_15;
  assign out_28 = out_16;
  assign out_29 = in_2[10];
  assign out_31 = in_2[6];
  assign out_32 = in_2[4];
  assign out_33 = in_2[2];
  assign out_34 = in_2[0];
  assign out_35 = i1;
  assign out_41 = in_2[10];
  assign out_43 = in_2[6];
  assign out_44 = in_2[4];
  assign out_45 = in_2[2];
  assign out_46 = in_2[0];
  assign out_49 = out_37;
  assign out_50 = out_38;
  assign out_51 = out_39;
  assign out_52 = out_40;
  assign out_53 = in_3[10];
  assign out_54 = in_3[8];
  assign out_55 = in_3[6];
  assign out_56 = in_3[4];
  assign out_57 = in_3[2];
  assign out_58 = in_3[0];
  assign out_65 = in_3[10];
  assign out_66 = in_3[8];
  assign out_67 = in_3[6];
  assign out_68 = in_3[4];
  assign out_69 = in_3[2];
  assign out_70 = in_3[0];
  assign out_71 = out_59;
  assign out_72 = out_60;
  assign out_73 = out_61;
  assign out_74 = out_62;
  assign out_75 = out_63;
  assign out_76 = out_64;
  assign out_77 = in_4[10];
  assign out_78 = in_4[8];
  assign out_79 = in_4[6];
  assign out_80 = in_4[4];
  assign out_81 = in_4[2];
  assign out_82 = in_4[0];
  assign out_89 = in_4[10];
  assign out_90 = in_4[8];
  assign out_91 = in_4[6];
  assign out_92 = in_4[4];
  assign out_93 = in_4[2];
  assign out_94 = in_4[0];
  assign out_95 = out_83;
  assign out_96 = out_84;
  assign out_97 = out_85;
  assign out_98 = out_86;
  assign out_99 = out_87;
  assign out_100 = out_88;

  // Notes on the sheet:
  //   i2
endmodule

module AttackProcessor (
  input  [1:0] ValueIn,
  input  [2:0] State,
  output [1:0] ValueOut
);

  wire and_1_out, and_2_out, and_3_out, and_4_out, or_1_out;

  and and_1 (and_1_out, ~State[2], State[0]);  // AND_Gate
  and and_2 (and_2_out, ValueIn[0], ~State[0]);  // AND_Gate
  and and_3 (and_3_out, State[0], State[2], ValueIn[0]);
  and and_4 (and_4_out, ~ValueIn[0], ValueIn[1]);  // AND_Gate
  or or_1 (or_1_out, and_1_out, and_2_out);
  or or_2 (ValueOut[1], and_3_out, and_4_out);
  and and_5 (ValueOut[0], ~ValueIn[1], or_1_out);  // AND_Gate
endmodule

module ShipCountManager (
  input  [1:0] Attack_Proc_or_Out,
  input  [2:0] State,
  input  [2:0] ShipCount,
  output Player,
  output [2:0] Out
);

  wire [3:0] and_2_out;
  wire [3:3] adder_4bit_1_result, not_1_out;

  and and_1 (and_2_out[3], Attack_Proc_or_Out[0], ~Attack_Proc_or_Out[1], State[0], State[2]);  // AND_Gate
  and and_2 (and_2_out[0], ~Attack_Proc_or_Out[1], State[0]);  // AND_Gate
  not not_1 (not_1_out[3], 1'b1);
  Adder_4bit adder_4bit_1 (
    .a({{3{and_2_out[3]}}, and_2_out[0]}), .b({not_1_out[3], ShipCount}),
    .Result({adder_4bit_1_result[3], Out}));

  assign Player = State[1];
endmodule
