// Logisim project circuitX.circ as structural Verilog: 1 circuit, main circuit main
module main (
  input  in_1,
  input  [11:0] in_2,
  input  [11:0] in_3,
  input  in_4,
  input  [1:0] in_5,
  input  [11:0] in_6,
  input  [11:0] in_7
);

  wire undriven, undriven_2, undriven_3, undriven_4, undriven_5, undriven_6, undriven_7, undriven_8,
       undriven_9, undriven_10, undriven_11, undriven_12, undriven_13, undriven_14, undriven_15;
  wire [1:1] undriven_16, undriven_17, undriven_18;
  wire [9:1] undriven_19;

  LED led_1 (.in(in_1));
  LED led_2 (.in(in_4));
  LED led_3 (.in(undriven_7));
  LED led_4 (.in(undriven_4));
  LED led_5 (.in(undriven));
  LED led_6 (.in(undriven_10));
  LED led_7 (.in(undriven_5));
  LED led_8 (.in(undriven_2));
  LED led_9 (.in(undriven_11));
  LED led_10 (.in(undriven_8));
  LED led_11 (.in(undriven_3));
  LED led_12 (.in(undriven_9));
  LED led_13 (.in(undriven_12));
  LED led_14 (.in(undriven_6));
  LED led_15 (.in(undriven_19[7]));
  LED led_16 (.in(undriven_19[5]));
  LED led_17 (.in(undriven_19[9]));
  LED led_18 (.in(undriven_13));
  LED led_19 (.in(undriven_16[1]));
  LED led_20 (.in(undriven_14));
  LED led_21 (.in(undriven_17[1]));
  LED led_22 (.in(undriven_18[1]));
  LED led_23 (.in(undriven_15));
  LED led_24 (.in(undriven_19[3]));
  LED led_25 (.in(undriven_19[1]));
  LED led_26 (.in(in_5[0]));
  LED led_27 (.in(in_5[1]));
  LED led_28 (.in(in_2[8]));
  LED led_29 (.in(in_2[10]));
  LED led_30 (.in(in_2[11]));
  LED led_31 (.in(in_2[9]));
  LED led_32 (.in(in_2[7]));
  LED led_33 (.in(in_2[0]));
  LED led_34 (.in(in_2[4]));
  LED led_35 (.in(in_2[6]));
  LED led_36 (.in(in_2[2]));
  LED led_37 (.in(in_2[3]));
  LED led_38 (.in(in_2[1]));
  LED led_39 (.in(in_2[5]));

  // Other names for the same wires on the sheet: c = in_1
endmodule
