// Logisim project Adder.circ as structural Verilog: 3 circuits, main circuit HalfAdder
module HalfAdder (
  input  a,
  input  b,
  output Sum,
  output R
);

  xor xor_1 (Sum, a, b);
  and and_1 (R, b, a);
endmodule

module FullAdder (
  input  Rin,
  input  a,
  input  b,
  output Rout,
  output Sum
);

  wire and_1_out, and_2_out, xor_1_out;

  xor xor_1 (xor_1_out, a, b);
  and and_1 (and_1_out, b, a);
  and and_2 (and_2_out, Rin, xor_1_out);
  xor xor_2 (Sum, xor_1_out, Rin);
  or or_1 (Rout, and_1_out, and_2_out);
endmodule

module Adder_4bit (
  input  [3:0] a,
  input  [3:0] b,
  output [3:0] Result
);

  wire fulladder_1_rout, fulladder_2_rout, halfadder_1_r;

  HalfAdder halfadder_1 (.a(a[0]), .b(b[0]), .Sum(Result[0]), .R(halfadder_1_r));
  FullAdder fulladder_1 (.Rin(halfadder_1_r), .a(a[1]), .b(b[1]), .Rout(fulladder_1_rout), .Sum(Result[1]));
  FullAdder fulladder_2 (.Rin(fulladder_1_rout), .a(a[2]), .b(b[2]), .Rout(fulladder_2_rout), .Sum(Result[2]));
  FullAdder fulladder_3 (.Rin(fulladder_2_rout), .a(a[3]), .b(b[3]), .Sum(Result[3]));  // open: Rout
endmodule
