// Logisim project FlipFlop.circ as structural Verilog: 3 circuits, main circuit Latch-Set-Clear
module Latch_Set_Clear (
  input  S,
  input  C,
  output nQ,
  output Q
);

  nor nor_1 (nQ, S, Q);
  nor nor_2 (Q, nQ, C);
endmodule

module Latch_Set_Clear_Sync (
  input  Clock,
  input  D,
  output nQ,
  output Q
);

  wire and_1_out, and_2_out;

  and and_1 (and_1_out, Clock, ~D);  // AND_Gate
  and and_2 (and_2_out, Clock, D);
  Latch_Set_Clear latch_set_clear_1 (.S(and_1_out), .C(and_2_out), .nQ(nQ), .Q(Q));
endmodule

module FlipFlopDT (
  input  D,
  input  Clock,
  output Q,
  output nQ
);

  wire latch_set_clear_sync_1_q, not_1_out;

  Latch_Set_Clear_Sync latch_set_clear_sync_1 (.Clock(Clock), .D(D), .Q(latch_set_clear_sync_1_q));  // open: nQ
  not not_1 (not_1_out, Clock);
  Latch_Set_Clear_Sync latch_set_clear_sync_2 (.Clock(not_1_out), .D(latch_set_clear_sync_1_q), .nQ(nQ), .Q(Q));
endmodule
