// Logisim project Register.circ as structural Verilog: 3 circuits, main circuit Register 2Bit
module Register_2Bit (
  input  [1:0] IN,
  input  Clock,
  output [1:0] Q
);

  FlipFlopDT flipflopdt_1 (.D(IN[0]), .Clock(Clock), .Q(Q[0]));  // open: nQ
  FlipFlopDT flipflopdt_2 (.D(IN[1]), .Clock(Clock), .Q(Q[1]));  // open: nQ
endmodule

module Memory (
  input  [5:0] Register_write,
  input  Clock,
  input  [1:0] Write_content,
  input  [5:0] Register_read,
  input  [2:0] State_write,
  input  B_C__Player_write,
  input  [2:0] Write_boat_count,
  output [11:0] D2_3,
  output [11:0] D2_2,
  output [11:0] D2_1,
  output [11:0] D2_0,
  output [11:0] D1_3,
  output [11:0] D1_2,
  output [11:0] D1_1,
  output [11:0] D1_0,
  output [1:0] Read_out,
  output [2:0] State_out,
  output [2:0] B_C__1_out,
  output [2:0] B_C__2_out
);

  wire and_1_out, and_2_out, and_3_out, and_4_out, and_5_out, and_6_out, and_7_out, and_8_out, and_9_out,
       and_10_out, and_11_out, and_12_out, and_13_out, and_14_out, and_15_out, and_16_out, and_17_out,
       and_18_out, and_19_out, and_20_out, and_21_out, and_22_out, and_23_out, and_24_out, and_25_out,
       and_26_out, and_27_out, and_28_out, and_29_out, and_30_out, and_31_out, and_32_out, and_33_out,
       and_34_out, and_35_out, and_36_out, and_37_out, and_38_out, and_39_out, and_40_out, and_41_out,
       and_42_out, and_43_out, and_44_out, and_45_out, and_46_out, and_47_out, and_48_out, and_49_out,
       and_50_out, and_51_out, and_52_out, and_53_out, and_54_out, and_55_out, and_56_out, and_57_out,
       and_58_out, and_59_out, and_60_out, and_61_out, and_62_out, and_63_out, and_64_out, and_65_out,
       and_66_out, clock_1_out, decoder_1_out_2, decoder_1_out_3, decoder_1_out_4, decoder_1_out_5,
       decoder_1_out_6, decoder_1_out_7, decoder_1_out_8, decoder_1_out_9, decoder_1_out_10,
       decoder_1_out_11, decoder_1_out_12, decoder_1_out_13, decoder_1_out_14, decoder_1_out_15,
       decoder_1_out_16, decoder_1_out_17, decoder_1_out_18, decoder_1_out_19, decoder_1_out_20,
       decoder_1_out_21, decoder_1_out_22, decoder_1_out_23, decoder_1_out_24, decoder_1_out_25,
       decoder_1_out_26, decoder_1_out_27, decoder_1_out_28, decoder_1_out_29, decoder_1_out_30,
       decoder_1_out_31, decoder_1_out_32, decoder_1_out_33, decoder_1_out_34, decoder_1_out_35,
       decoder_1_out_36, decoder_1_out_37, decoder_1_out_38, decoder_1_out_39, decoder_1_out_40,
       decoder_1_out_41, decoder_1_out_42, decoder_1_out_43, decoder_1_out_44, decoder_1_out_45,
       decoder_1_out_46, decoder_1_out_47, decoder_1_out_48, decoder_1_out_49, decoder_1_out_50,
       decoder_1_out_51, decoder_1_out_52, decoder_1_out_53, decoder_1_out_54, decoder_1_out_55,
       decoder_1_out_56, decoder_1_out_57, decoder_1_out_58, decoder_1_out_59, decoder_1_out_60,
       decoder_1_out_61, decoder_1_out_62, decoder_1_out_63, decoder_1_out_64, decoder_1_out_65;
  wire [1:0] register_2bit_1_q, register_2bit_2_q, register_2bit_9_q, register_2bit_10_q, register_2bit_17_q,
       register_2bit_18_q, register_2bit_25_q, register_2bit_26_q, register_2bit_33_q, register_2bit_34_q,
       register_2bit_41_q, register_2bit_42_q, register_2bit_49_q, register_2bit_50_q, register_2bit_57_q,
       register_2bit_58_q;

  Decoder decoder_1 (
    .in_1(Register_write), .out_2(decoder_1_out_2), .out_3(decoder_1_out_3), .out_4(decoder_1_out_4),
    .out_5(decoder_1_out_5), .out_6(decoder_1_out_6), .out_7(decoder_1_out_7), .out_8(decoder_1_out_8),
    .out_9(decoder_1_out_9), .out_10(decoder_1_out_10), .out_11(decoder_1_out_11), .out_12(decoder_1_out_12),
    .out_13(decoder_1_out_13), .out_14(decoder_1_out_14), .out_15(decoder_1_out_15),
    .out_16(decoder_1_out_16), .out_17(decoder_1_out_17), .out_18(decoder_1_out_18),
    .out_19(decoder_1_out_19), .out_20(decoder_1_out_20), .out_21(decoder_1_out_21),
    .out_22(decoder_1_out_22), .out_23(decoder_1_out_23), .out_24(decoder_1_out_24),
    .out_25(decoder_1_out_25), .out_26(decoder_1_out_26), .out_27(decoder_1_out_27),
    .out_28(decoder_1_out_28), .out_29(decoder_1_out_29), .out_30(decoder_1_out_30),
    .out_31(decoder_1_out_31), .out_32(decoder_1_out_32), .out_33(decoder_1_out_33),
    .out_34(decoder_1_out_34), .out_35(decoder_1_out_35), .out_36(decoder_1_out_36),
    .out_37(decoder_1_out_37), .out_38(decoder_1_out_38), .out_39(decoder_1_out_39),
    .out_40(decoder_1_out_40), .out_41(decoder_1_out_41), .out_42(decoder_1_out_42),
    .out_43(decoder_1_out_43), .out_44(decoder_1_out_44), .out_45(decoder_1_out_45),
    .out_46(decoder_1_out_46), .out_47(decoder_1_out_47), .out_48(decoder_1_out_48),
    .out_49(decoder_1_out_49), .out_50(decoder_1_out_50), .out_51(decoder_1_out_51),
    .out_52(decoder_1_out_52), .out_53(decoder_1_out_53), .out_54(decoder_1_out_54),
    .out_55(decoder_1_out_55), .out_56(decoder_1_out_56), .out_57(decoder_1_out_57),
    .out_58(decoder_1_out_58), .out_59(decoder_1_out_59), .out_60(decoder_1_out_60),
    .out_61(decoder_1_out_61), .out_62(decoder_1_out_62), .out_63(decoder_1_out_63),
    .out_64(decoder_1_out_64), .out_65(decoder_1_out_65));
  Clock clock_1 (.out(clock_1_out));
  and and_1 (and_1_out, decoder_1_out_65, clock_1_out);
  and and_2 (and_2_out, decoder_1_out_64, clock_1_out);
  and and_3 (and_3_out, decoder_1_out_63, clock_1_out);
  and and_4 (and_4_out, decoder_1_out_62, clock_1_out);
  and and_5 (and_5_out, decoder_1_out_61, clock_1_out);
  and and_6 (and_6_out, decoder_1_out_60, clock_1_out);
  and and_7 (and_7_out, decoder_1_out_59, clock_1_out);
  and and_8 (and_8_out, decoder_1_out_58, clock_1_out);
  and and_9 (and_9_out, decoder_1_out_57, clock_1_out);
  and and_10 (and_10_out, decoder_1_out_56, clock_1_out);
  and and_11 (and_11_out, decoder_1_out_55, clock_1_out);
  and and_12 (and_12_out, decoder_1_out_54, clock_1_out);
  and and_13 (and_13_out, decoder_1_out_53, clock_1_out);
  and and_14 (and_14_out, decoder_1_out_52, clock_1_out);
  and and_15 (and_15_out, decoder_1_out_51, clock_1_out);
  and and_16 (and_16_out, decoder_1_out_50, clock_1_out);
  and and_17 (and_17_out, decoder_1_out_49, clock_1_out);
  and and_18 (and_18_out, decoder_1_out_48, clock_1_out);
  and and_19 (and_19_out, decoder_1_out_47, clock_1_out);
  and and_20 (and_20_out, decoder_1_out_46, clock_1_out);
  and and_21 (and_21_out, decoder_1_out_45, clock_1_out);
  and and_22 (and_22_out, decoder_1_out_44, clock_1_out);
  and and_23 (and_23_out, decoder_1_out_43, clock_1_out);
  and and_24 (and_24_out, decoder_1_out_42, clock_1_out);
  and and_25 (and_25_out, decoder_1_out_41, clock_1_out);
  and and_26 (and_26_out, decoder_1_out_40, clock_1_out);
  and and_27 (and_27_out, decoder_1_out_39, clock_1_out);
  and and_28 (and_28_out, decoder_1_out_38, clock_1_out);
  and and_29 (and_29_out, decoder_1_out_37, clock_1_out);
  and and_30 (and_30_out, decoder_1_out_36, clock_1_out);
  and and_31 (and_31_out, decoder_1_out_35, clock_1_out);
  and and_32 (and_32_out, decoder_1_out_34, clock_1_out);
  and and_33 (and_33_out, decoder_1_out_33, clock_1_out);
  and and_34 (and_34_out, decoder_1_out_32, clock_1_out);
  and and_35 (and_35_out, decoder_1_out_31, clock_1_out);
  and and_36 (and_36_out, decoder_1_out_30, clock_1_out);
  and and_37 (and_37_out, decoder_1_out_29, clock_1_out);
  and and_38 (and_38_out, decoder_1_out_28, clock_1_out);
  and and_39 (and_39_out, decoder_1_out_27, clock_1_out);
  and and_40 (and_40_out, decoder_1_out_26, clock_1_out);
  and and_41 (and_41_out, decoder_1_out_25, clock_1_out);
  and and_42 (and_42_out, decoder_1_out_24, clock_1_out);
  and and_43 (and_43_out, decoder_1_out_23, clock_1_out);
  and and_44 (and_44_out, decoder_1_out_22, clock_1_out);
  and and_45 (and_45_out, decoder_1_out_21, clock_1_out);
  and and_46 (and_46_out, decoder_1_out_20, clock_1_out);
  and and_47 (and_47_out, decoder_1_out_19, clock_1_out);
  and and_48 (and_48_out, decoder_1_out_18, clock_1_out);
  and and_49 (and_49_out, decoder_1_out_17, clock_1_out);
  and and_50 (and_50_out, decoder_1_out_16, clock_1_out);
  and and_51 (and_51_out, decoder_1_out_15, clock_1_out);
  and and_52 (and_52_out, decoder_1_out_14, clock_1_out);
  and and_53 (and_53_out, decoder_1_out_13, clock_1_out);
  and and_54 (and_54_out, decoder_1_out_12, clock_1_out);
  and and_55 (and_55_out, decoder_1_out_11, clock_1_out);
  and and_56 (and_56_out, decoder_1_out_10, clock_1_out);
  and and_57 (and_57_out, decoder_1_out_9, clock_1_out);
  and and_58 (and_58_out, decoder_1_out_8, clock_1_out);
  and and_59 (and_59_out, decoder_1_out_7, clock_1_out);
  and and_60 (and_60_out, decoder_1_out_6, clock_1_out);
  and and_61 (and_61_out, decoder_1_out_5, clock_1_out);
  and and_62 (and_62_out, decoder_1_out_4, clock_1_out);
  and and_63 (and_63_out, decoder_1_out_3, clock_1_out);
  and and_64 (and_64_out, decoder_1_out_2, clock_1_out);
  and and_65 (and_65_out, ~B_C__Player_write, clock_1_out);  // AND_Gate
  and and_66 (and_66_out, B_C__Player_write, clock_1_out);
  Register_2Bit register_2bit_1 (.IN(Write_content), .Clock(and_1_out), .Q(register_2bit_1_q));
  Register_2Bit register_2bit_2 (.IN(Write_content), .Clock(and_2_out), .Q(register_2bit_2_q));
  Register_2Bit register_2bit_3 (.IN(Write_content), .Clock(and_3_out), .Q({D2_3[0], D2_3[1]}));
  Register_2Bit register_2bit_4 (.IN(Write_content), .Clock(and_4_out), .Q({D2_3[2], D2_3[3]}));
  Register_2Bit register_2bit_5 (.IN(Write_content), .Clock(and_5_out), .Q({D2_3[4], D2_3[5]}));
  Register_2Bit register_2bit_6 (.IN(Write_content), .Clock(and_6_out), .Q({D2_3[6], D2_3[7]}));
  Register_2Bit register_2bit_7 (.IN(Write_content), .Clock(and_7_out), .Q({D2_3[8], D2_3[9]}));
  Register_2Bit register_2bit_8 (.IN(Write_content), .Clock(and_8_out), .Q({D2_3[10], D2_3[11]}));
  Register_2Bit register_2bit_9 (.IN(Write_content), .Clock(and_9_out), .Q(register_2bit_9_q));
  Register_2Bit register_2bit_10 (.IN(Write_content), .Clock(and_10_out), .Q(register_2bit_10_q));
  Register_2Bit register_2bit_11 (.IN(Write_content), .Clock(and_11_out), .Q({D2_2[0], D2_2[1]}));
  Register_2Bit register_2bit_12 (.IN(Write_content), .Clock(and_12_out), .Q({D2_2[2], D2_2[3]}));
  Register_2Bit register_2bit_13 (.IN(Write_content), .Clock(and_13_out), .Q({D2_2[4], D2_2[5]}));
  Register_2Bit register_2bit_14 (.IN(Write_content), .Clock(and_14_out), .Q({D2_2[6], D2_2[7]}));
  Register_2Bit register_2bit_15 (.IN(Write_content), .Clock(and_15_out), .Q({D2_2[8], D2_2[9]}));
  Register_2Bit register_2bit_16 (.IN(Write_content), .Clock(and_16_out), .Q({D2_2[10], D2_2[11]}));
  Register_2Bit register_2bit_17 (.IN(Write_content), .Clock(and_17_out), .Q(register_2bit_17_q));
  Register_2Bit register_2bit_18 (.IN(Write_content), .Clock(and_18_out), .Q(register_2bit_18_q));
  Register_2Bit register_2bit_19 (.IN(Write_content), .Clock(and_19_out), .Q({D2_1[0], D2_1[1]}));
  Register_2Bit register_2bit_20 (.IN(Write_content), .Clock(and_20_out), .Q({D2_1[2], D2_1[3]}));
  Register_2Bit register_2bit_21 (.IN(Write_content), .Clock(and_21_out), .Q({D2_1[4], D2_1[5]}));
  Register_2Bit register_2bit_22 (.IN(Write_content), .Clock(and_22_out), .Q({D2_1[6], D2_1[7]}));
  Register_2Bit register_2bit_23 (.IN(Write_content), .Clock(and_23_out), .Q({D2_1[8], D2_1[9]}));
  Register_2Bit register_2bit_24 (.IN(Write_content), .Clock(and_24_out), .Q({D2_1[10], D2_1[11]}));
  Register_2Bit register_2bit_25 (.IN(Write_content), .Clock(and_25_out), .Q(register_2bit_25_q));
  Register_2Bit register_2bit_26 (.IN(Write_content), .Clock(and_26_out), .Q(register_2bit_26_q));
  Register_2Bit register_2bit_27 (.IN(Write_content), .Clock(and_27_out), .Q({D2_0[0], D2_0[1]}));
  Register_2Bit register_2bit_28 (.IN(Write_content), .Clock(and_28_out), .Q({D2_0[2], D2_0[3]}));
  Register_2Bit register_2bit_29 (.IN(Write_content), .Clock(and_29_out), .Q({D2_0[4], D2_0[5]}));
  Register_2Bit register_2bit_30 (.IN(Write_content), .Clock(and_30_out), .Q({D2_0[6], D2_0[7]}));
  Register_2Bit register_2bit_31 (.IN(Write_content), .Clock(and_31_out), .Q({D2_0[8], D2_0[9]}));
  Register_2Bit register_2bit_32 (.IN(Write_content), .Clock(and_32_out), .Q({D2_0[10], D2_0[11]}));
  Register_2Bit register_2bit_33 (.IN(Write_content), .Clock(and_33_out), .Q(register_2bit_33_q));
  Register_2Bit register_2bit_34 (.IN(Write_content), .Clock(and_34_out), .Q(register_2bit_34_q));
  Register_2Bit register_2bit_35 (.IN(Write_content), .Clock(and_35_out), .Q({D1_3[0], D1_3[1]}));
  Register_2Bit register_2bit_36 (.IN(Write_content), .Clock(and_36_out), .Q({D1_3[2], D1_3[3]}));
  Register_2Bit register_2bit_37 (.IN(Write_content), .Clock(and_37_out), .Q({D1_3[4], D1_3[5]}));
  Register_2Bit register_2bit_38 (.IN(Write_content), .Clock(and_38_out), .Q({D1_3[6], D1_3[7]}));
  Register_2Bit register_2bit_39 (.IN(Write_content), .Clock(and_39_out), .Q({D1_3[8], D1_3[9]}));
  Register_2Bit register_2bit_40 (.IN(Write_content), .Clock(and_40_out), .Q({D1_3[10], D1_3[11]}));
  Register_2Bit register_2bit_41 (.IN(Write_content), .Clock(and_41_out), .Q(register_2bit_41_q));
  Register_2Bit register_2bit_42 (.IN(Write_content), .Clock(and_42_out), .Q(register_2bit_42_q));
  Register_2Bit register_2bit_43 (.IN(Write_content), .Clock(and_43_out), .Q({D1_2[0], D1_2[1]}));
  Register_2Bit register_2bit_44 (.IN(Write_content), .Clock(and_44_out), .Q({D1_2[2], D1_2[3]}));
  Register_2Bit register_2bit_45 (.IN(Write_content), .Clock(and_45_out), .Q({D1_2[4], D1_2[5]}));
  Register_2Bit register_2bit_46 (.IN(Write_content), .Clock(and_46_out), .Q({D1_2[6], D1_2[7]}));
  Register_2Bit register_2bit_47 (.IN(Write_content), .Clock(and_47_out), .Q({D1_2[8], D1_2[9]}));
  Register_2Bit register_2bit_48 (.IN(Write_content), .Clock(and_48_out), .Q({D1_2[10], D1_2[11]}));
  Register_2Bit register_2bit_49 (.IN(Write_content), .Clock(and_49_out), .Q(register_2bit_49_q));
  Register_2Bit register_2bit_50 (.IN(Write_content), .Clock(and_50_out), .Q(register_2bit_50_q));
  Register_2Bit register_2bit_51 (.IN(Write_content), .Clock(and_51_out), .Q({D1_1[0], D1_1[1]}));
  Register_2Bit register_2bit_52 (.IN(Write_content), .Clock(and_52_out), .Q({D1_1[2], D1_1[3]}));
  Register_2Bit register_2bit_53 (.IN(Write_content), .Clock(and_53_out), .Q({D1_1[4], D1_1[5]}));
  Register_2Bit register_2bit_54 (.IN(Write_content), .Clock(and_54_out), .Q({D1_1[6], D1_1[7]}));
  Register_2Bit register_2bit_55 (.IN(Write_content), .Clock(and_55_out), .Q({D1_1[8], D1_1[9]}));
  Register_2Bit register_2bit_56 (.IN(Write_content), .Clock(and_56_out), .Q({D1_1[10], D1_1[11]}));
  Register_2Bit register_2bit_57 (.IN(Write_content), .Clock(and_57_out), .Q(register_2bit_57_q));
  Register_2Bit register_2bit_58 (.IN(Write_content), .Clock(and_58_out), .Q(register_2bit_58_q));
  Register_2Bit register_2bit_59 (.IN(Write_content), .Clock(and_59_out), .Q({D1_0[0], D1_0[1]}));
  Register_2Bit register_2bit_60 (.IN(Write_content), .Clock(and_60_out), .Q({D1_0[2], D1_0[3]}));
  Register_2Bit register_2bit_61 (.IN(Write_content), .Clock(and_61_out), .Q({D1_0[4], D1_0[5]}));
  Register_2Bit register_2bit_62 (.IN(Write_content), .Clock(and_62_out), .Q({D1_0[6], D1_0[7]}));
  Register_2Bit register_2bit_63 (.IN(Write_content), .Clock(and_63_out), .Q({D1_0[8], D1_0[9]}));
  Register_2Bit register_2bit_64 (.IN(Write_content), .Clock(and_64_out), .Q({D1_0[10], D1_0[11]}));
  Register_3Bit register_3bit_1 (.IN(State_write), .Clock(clock_1_out), .OUT(State_out));
  Register_3Bit register_3bit_2 (.IN(Write_boat_count), .Clock(and_65_out), .OUT(B_C__1_out));
  Register_3Bit register_3bit_3 (.IN(Write_boat_count), .Clock(and_66_out), .OUT(B_C__2_out));
  Multiplexer_64 multiplexer_64_1 (
    .out_66(Read_out), .in_1({D1_0[10], D1_0[11]}), .in_2({D1_0[8], D1_0[9]}), .in_3({D1_0[6], D1_0[7]}),
    .in_4({D1_0[4], D1_0[5]}), .in_5({D1_0[2], D1_0[3]}), .in_6({D1_0[0], D1_0[1]}),
    .in_7(register_2bit_58_q), .in_8(register_2bit_57_q), .in_9({D1_1[10], D1_1[11]}),
    .in_10({D1_1[8], D1_1[9]}), .in_11({D1_1[6], D1_1[7]}), .in_12({D1_1[4], D1_1[5]}),
    .in_13({D1_1[2], D1_1[3]}), .in_14({D1_1[0], D1_1[1]}), .in_15(register_2bit_50_q),
    .in_16(register_2bit_49_q), .in_17({D1_2[10], D1_2[11]}), .in_18({D1_2[8], D1_2[9]}),
    .in_19({D1_2[6], D1_2[7]}), .in_20({D1_2[4], D1_2[5]}), .in_21({D1_2[2], D1_2[3]}),
    .in_22({D1_2[0], D1_2[1]}), .in_23(register_2bit_42_q), .in_24(register_2bit_41_q),
    .in_25({D1_3[10], D1_3[11]}), .in_26({D1_3[8], D1_3[9]}), .in_27({D1_3[6], D1_3[7]}),
    .in_28({D1_3[4], D1_3[5]}), .in_29({D1_3[2], D1_3[3]}), .in_30({D1_3[0], D1_3[1]}),
    .in_31(register_2bit_34_q), .in_32(register_2bit_33_q), .in_33({D2_0[10], D2_0[11]}),
    .in_34({D2_0[8], D2_0[9]}), .in_35({D2_0[6], D2_0[7]}), .in_36({D2_0[4], D2_0[5]}),
    .in_37({D2_0[2], D2_0[3]}), .in_38({D2_0[0], D2_0[1]}), .in_39(register_2bit_26_q),
    .in_40(register_2bit_25_q), .in_41({D2_1[10], D2_1[11]}), .in_42({D2_1[8], D2_1[9]}),
    .in_43({D2_1[6], D2_1[7]}), .in_44({D2_1[4], D2_1[5]}), .in_45({D2_1[2], D2_1[3]}),
    .in_46({D2_1[0], D2_1[1]}), .in_47(register_2bit_18_q), .in_48(register_2bit_17_q),
    .in_49({D2_2[10], D2_2[11]}), .in_50({D2_2[8], D2_2[9]}), .in_51({D2_2[6], D2_2[7]}),
    .in_52({D2_2[4], D2_2[5]}), .in_53({D2_2[2], D2_2[3]}), .in_54({D2_2[0], D2_2[1]}),
    .in_55(register_2bit_10_q), .in_56(register_2bit_9_q), .in_57({D2_3[10], D2_3[11]}),
    .in_58({D2_3[8], D2_3[9]}), .in_59({D2_3[6], D2_3[7]}), .in_60({D2_3[4], D2_3[5]}),
    .in_61({D2_3[2], D2_3[3]}), .in_62({D2_3[0], D2_3[1]}), .in_63(register_2bit_2_q),
    .in_64(register_2bit_1_q), .Select(Register_read));

  // Notes on the sheet:
  //   Grid Memory
  //   State
  //   Boat count player 1
  //   Boat count player 2
  //   |------------------------------------------- Display out 2 ----------------------------------------------|
  //   |------------------------------------------- Display out 1 ----------------------------------------------|
endmodule

module Register_3Bit (
  input  [2:0] IN,
  input  Clock,
  output [2:0] OUT
);

  FlipFlopDT flipflopdt_1 (.D(IN[0]), .Clock(Clock), .Q(OUT[0]));  // open: nQ
  FlipFlopDT flipflopdt_2 (.D(IN[1]), .Clock(Clock), .Q(OUT[1]));  // open: nQ
  FlipFlopDT flipflopdt_3 (.D(IN[2]), .Clock(Clock), .Q(OUT[2]));  // open: nQ
endmodule
